// Logisim project 电路.circ as structural Verilog: 22 circuits, main circuit 实验1：七段数码管
module \实验1_七段数码管  (
  input  \阴阳控制器 
);

  wire dipswitch_1_p1, dipswitch_1_p2, dipswitch_1_p3, dipswitch_1_p4, \七段数码管译码器_1_a_2 , \七段数码管译码器_1_b ,
       \七段数码管译码器_1_c , \七段数码管译码器_1_d , \七段数码管译码器_1_e , \七段数码管译码器_1_f , \七段数码管译码器_1_g , \七段数码管译码器_1_h ;

  // DipSwitch #(.NSwitches(4)) dipswitch_1: pin names not known; wires that end beside it: dipswitch_1_p1, dipswitch_1_p2, dipswitch_1_p3, dipswitch_1_p4
  \七段数码管译码器  \u_七段数码管译码器_1  (
    .A(\阴阳控制器 ), .A3(dipswitch_1_p1), .A2(dipswitch_1_p2), .A1(dipswitch_1_p3), .A0(dipswitch_1_p4),
    .a_2(\七段数码管译码器_1_a_2 ), .b(\七段数码管译码器_1_b ), .c(\七段数码管译码器_1_c ), .d(\七段数码管译码器_1_d ), .e(\七段数码管译码器_1_e ),
    .f(\七段数码管译码器_1_f ), .g(\七段数码管译码器_1_g ), .h(\七段数码管译码器_1_h ));
  _7_Segment_Display #(.active("true")) u_7_segment_display_1 (
    .g(\七段数码管译码器_1_g ), .f(\七段数码管译码器_1_f ), .a(\七段数码管译码器_1_a_2 ), .b(\七段数码管译码器_1_b ), .e(\七段数码管译码器_1_e ),
    .d(\七段数码管译码器_1_d ), .c(\七段数码管译码器_1_c ), .dp(\七段数码管译码器_1_h ));
endmodule

module \七段数码管译码器  (
  input  A,
  input  A3,
  input  A2,
  input  A1,
  input  A0,
  output a_2,
  output b,
  output c,
  output d,
  output e,
  output f,
  output g,
  output h
);

  wire and_1_out, and_2_out, and_3_out, and_4_out, and_5_out, and_6_out, and_7_out, and_8_out, and_9_out,
       and_10_out, and_11_out, and_12_out, and_13_out, and_14_out, and_15_out, and_16_out, and_17_out,
       and_18_out, and_19_out, and_20_out, and_21_out, and_22_out, and_23_out, and_24_out, and_25_out,
       and_26_out, and_27_out, and_28_out, and_29_out, and_30_out, and_31_out, and_32_out, and_33_out,
       and_34_out, and_35_out, and_36_out, and_37_out, and_38_out, and_39_out, and_40_out, and_41_out,
       and_42_out, and_43_out, and_44_out, and_45_out, and_46_out, and_47_out, and_48_out, and_49_out,
       and_50_out, and_51_out, and_52_out, and_53_out, not_1_out, not_2_out, not_3_out, not_4_out, not_5_out,
       not_6_out, not_7_out, not_8_out, not_9_out, not_10_out, not_11_out, not_12_out, not_13_out,
       not_14_out, not_15_out, not_16_out, not_17_out, not_18_out, not_19_out, not_20_out, not_21_out,
       not_22_out, not_23_out, not_24_out, not_25_out, not_26_out, not_27_out, not_28_out, not_29_out,
       not_30_out, not_31_out, not_32_out, not_33_out, not_34_out, not_35_out, not_36_out, not_37_out,
       not_38_out, not_39_out, not_40_out, not_41_out, not_42_out, not_43_out, not_44_out, not_45_out,
       not_46_out, not_47_out, not_48_out, not_49_out, not_50_out, not_51_out, not_52_out, not_53_out,
       not_54_out, not_55_out, not_56_out, not_57_out, not_58_out, not_59_out, not_60_out, not_61_out,
       not_62_out, not_63_out, not_64_out, not_65_out, not_66_out, not_67_out, not_68_out, not_69_out,
       not_70_out, not_71_out, not_72_out, not_73_out, not_74_out, not_75_out, not_76_out, not_77_out,
       not_78_out, not_79_out, not_80_out, not_81_out, not_82_out, not_83_out, not_84_out, not_85_out,
       not_86_out, not_87_out, not_88_out, not_89_out, not_90_out, not_91_out, not_92_out, not_93_out,
       not_94_out, not_95_out, not_96_out, not_97_out, not_98_out, not_99_out;

  not not_1 (not_1_out, A);
  not not_2 (not_2_out, A3);
  not not_3 (not_3_out, A2);
  not not_4 (not_4_out, A0);
  not not_5 (not_5_out, A);
  not not_6 (not_6_out, A3);
  not not_7 (not_7_out, A);
  not not_8 (not_8_out, A2);
  not not_9 (not_9_out, A1);
  not not_10 (not_10_out, A3);
  not not_11 (not_11_out, A2);
  not not_12 (not_12_out, A1);
  not not_13 (not_13_out, A1);
  not not_14 (not_14_out, A0);
  not not_15 (not_15_out, A);
  not not_16 (not_16_out, A3);
  not not_17 (not_17_out, A1);
  not not_18 (not_18_out, A0);
  not not_19 (not_19_out, A);
  not not_20 (not_20_out, A3);
  not not_21 (not_21_out, A1);
  not not_22 (not_22_out, A0);
  not not_23 (not_23_out, A2);
  not not_24 (not_24_out, A0);
  not not_25 (not_25_out, A);
  not not_26 (not_26_out, A3);
  not not_27 (not_27_out, A2);
  not not_28 (not_28_out, A0);
  not not_29 (not_29_out, A);
  not not_30 (not_30_out, A3);
  not not_31 (not_31_out, A2);
  not not_32 (not_32_out, A);
  not not_33 (not_33_out, A3);
  not not_34 (not_34_out, A0);
  not not_35 (not_35_out, A);
  not not_36 (not_36_out, A3);
  not not_37 (not_37_out, A1);
  not not_38 (not_38_out, A);
  not not_39 (not_39_out, A2);
  not not_40 (not_40_out, A1);
  not not_41 (not_41_out, A3);
  not not_42 (not_42_out, A2);
  not not_43 (not_43_out, A1);
  not not_44 (not_44_out, A1);
  not not_45 (not_45_out, A0);
  not not_46 (not_46_out, A);
  not not_47 (not_47_out, A2);
  not not_48 (not_48_out, A1);
  not not_49 (not_49_out, A0);
  not not_50 (not_50_out, A);
  not not_51 (not_51_out, A3);
  not not_52 (not_52_out, A0);
  not not_53 (not_53_out, A);
  not not_54 (not_54_out, A3);
  not not_55 (not_55_out, A1);
  not not_56 (not_56_out, A0);
  not not_57 (not_57_out, A);
  not not_58 (not_58_out, A3);
  not not_59 (not_59_out, A1);
  not not_60 (not_60_out, A);
  not not_61 (not_61_out, A3);
  not not_62 (not_62_out, A0);
  not not_63 (not_63_out, A);
  not not_64 (not_64_out, A2);
  not not_65 (not_65_out, A1);
  not not_66 (not_66_out, A3);
  not not_67 (not_67_out, A2);
  not not_68 (not_68_out, A);
  not not_69 (not_69_out, A3);
  not not_70 (not_70_out, A2);
  not not_71 (not_71_out, A);
  not not_72 (not_72_out, A3);
  not not_73 (not_73_out, A1);
  not not_74 (not_74_out, A);
  not not_75 (not_75_out, A3);
  not not_76 (not_76_out, A0);
  not not_77 (not_77_out, A);
  not not_78 (not_78_out, A2);
  not not_79 (not_79_out, A1);
  not not_80 (not_80_out, A3);
  not not_81 (not_81_out, A2);
  not not_82 (not_82_out, A1);
  and and_1 (and_1_out, not_1_out, not_2_out, not_3_out, not_4_out);
  not not_83 (not_83_out, A);
  and and_2 (and_2_out, not_83_out, not_84_out, A1);
  not not_84 (not_84_out, A3);
  and and_3 (and_3_out, not_5_out, not_6_out, A2, A0);
  and and_4 (and_4_out, not_7_out, A3, not_8_out, not_9_out);
  and and_5 (and_5_out, A, not_10_out, not_11_out, not_12_out, A0);
  and and_6 (and_6_out, A, A2, not_13_out, not_14_out);
  and and_7 (and_7_out, A, A3, A1);
  and and_8 (and_8_out, A, A3, A2);
  not not_85 (not_85_out, A);
  not not_86 (not_86_out, A3);
  and and_9 (and_9_out, not_85_out, not_86_out, not_87_out);
  not not_87 (not_87_out, A2);
  and and_10 (and_10_out, not_15_out, not_16_out, not_17_out, not_18_out);
  not not_88 (not_88_out, A);
  and and_11 (and_11_out, not_88_out, not_89_out, not_90_out);
  not not_89 (not_89_out, A2);
  not not_90 (not_90_out, A1);
  and and_12 (and_12_out, not_19_out, not_20_out, A1, A0);
  and and_13 (and_13_out, A, A2, not_21_out, A0);
  and and_14 (and_14_out, A, A2, A1, not_22_out);
  and and_15 (and_15_out, A, A3, A1);
  and and_16 (and_16_out, A, A3, A2);
  not not_91 (not_91_out, A);
  and and_17 (and_17_out, not_91_out, not_92_out, not_93_out);
  not not_92 (not_92_out, A2);
  not not_93 (not_93_out, A1);
  not not_94 (not_94_out, A);
  not not_95 (not_95_out, A3);
  and and_18 (and_18_out, not_94_out, not_95_out, A0);
  not not_96 (not_96_out, A);
  not not_97 (not_97_out, A3);
  and and_19 (and_19_out, not_96_out, not_97_out, A2);
  and and_20 (and_20_out, A, not_23_out, A1, not_24_out);
  and and_21 (and_21_out, A, A3, A1);
  and and_22 (and_22_out, A, A3, A2);
  and and_23 (and_23_out, not_25_out, not_26_out, not_27_out, not_28_out);
  and and_24 (and_24_out, not_29_out, not_30_out, not_31_out, A1);
  and and_25 (and_25_out, not_32_out, not_33_out, A1, not_34_out);
  and and_26 (and_26_out, not_35_out, not_36_out, A2, not_37_out, A0);
  and and_27 (and_27_out, not_38_out, A3, not_39_out, not_40_out);
  and and_28 (and_28_out, A, not_41_out, not_42_out, not_43_out, A0);
  and and_29 (and_29_out, A, A2, not_44_out, not_45_out);
  and and_30 (and_30_out, A, A2, A1, A0);
  and and_31 (and_31_out, A, A3, A1);
  and and_32 (and_32_out, A, A3, A2);
  and and_33 (and_33_out, not_46_out, not_47_out, not_48_out, not_49_out);
  and and_34 (and_34_out, not_50_out, not_51_out, A1, not_52_out);
  and and_35 (and_35_out, A, A0);
  and and_36 (and_36_out, A, A2, not_98_out);
  not not_98 (not_98_out, A1);
  and and_37 (and_37_out, A, A3, A1);
  and and_38 (and_38_out, not_53_out, not_54_out, not_55_out, not_56_out);
  and and_39 (and_39_out, not_57_out, not_58_out, A2, not_59_out);
  and and_40 (and_40_out, not_60_out, not_61_out, A2, not_62_out);
  and and_41 (and_41_out, not_63_out, A3, not_64_out, not_65_out);
  and and_42 (and_42_out, A, not_66_out, not_67_out, A0);
  and and_43 (and_43_out, A, not_99_out, A1);
  not not_99 (not_99_out, A2);
  and and_44 (and_44_out, A, A1, A0);
  and and_45 (and_45_out, A, A3, A2);
  and and_46 (and_46_out, not_68_out, not_69_out, not_70_out, A1);
  and and_47 (and_47_out, not_71_out, not_72_out, A2, not_73_out);
  and and_48 (and_48_out, not_74_out, not_75_out, A2, not_76_out);
  and and_49 (and_49_out, not_77_out, A3, not_78_out, not_79_out);
  and and_50 (and_50_out, A, not_80_out, not_81_out, not_82_out);
  and and_51 (and_51_out, A, A2, A1, A0);
  and and_52 (and_52_out, A, A3, A1);
  and and_53 (and_53_out, A, A3, A2);
  or or_1 (e, and_33_out, and_34_out, and_35_out, and_36_out, and_37_out);
  or or_2 (a_2, and_1_out, and_2_out, and_3_out, and_4_out, and_5_out, and_6_out, and_7_out, and_8_out);
  or or_3 (b, and_9_out, and_10_out, and_11_out, and_12_out, and_13_out, and_14_out, and_15_out, and_16_out);
  or or_4 (c, and_17_out, and_18_out, and_19_out, and_20_out, and_21_out, and_22_out);
  or or_5 (d, and_23_out, and_24_out, and_25_out, and_26_out, and_27_out, and_28_out, and_29_out, and_30_out, and_31_out, and_32_out);
  or or_6 (f, and_38_out, and_39_out, and_40_out, and_41_out, and_42_out, and_43_out, and_44_out, and_45_out);
  or or_7 (g, and_46_out, and_47_out, and_48_out, and_49_out, and_50_out, and_51_out, and_52_out, and_53_out);

  assign h = A;
endmodule

module \交通控制灯  (
  input  TA,
  input  TB,
  input  in_3
);

  wire and_1_out, and_2_out, and_3_out, and_4_out, and_5_out, and_6_out, and_7_out, and_8_out, and_9_out,
       and_10_out, clock_1_out, not_1_out, not_2_out, not_3_out, not_4_out, not_5_out, not_6_out, not_7_out,
       not_8_out, not_9_out, not_10_out, not_11_out, not_12_out, not_13_out, not_14_out, not_15_out;
  wire [1:0] or_1_out, register_1_q;

  not not_1 (not_1_out, register_1_q[1]);
  not not_2 (not_2_out, register_1_q[0]);
  not not_3 (not_3_out, TA);
  not not_4 (not_4_out, register_1_q[0]);
  not not_5 (not_5_out, TB);
  and and_1 (and_1_out, not_1_out, not_2_out, not_3_out);
  and and_2 (and_2_out, register_1_q[1], not_4_out, not_5_out);
  xor xor_1 (or_1_out[1], register_1_q[1], register_1_q[0]);
  or or_1 (or_1_out[0], and_1_out, and_2_out);
  Clock #(.highDuration(1), .lowDuration(1)) clock_1 (.out(clock_1_out));
  Register #(.width(2), .trigger("rising"), .Select("low")) register_1 (
    .D(or_1_out), .Q(register_1_q), .clk(clock_1_out), .clr(in_3));  // open: en
  not not_6 (not_6_out, register_1_q[1]);
  and and_3 (and_3_out, not_6_out, register_1_q[0]);
  not not_7 (not_7_out, register_1_q[1]);
  and and_4 (and_4_out, register_1_q[0], register_1_q[1]);
  LED #(.active("true")) led_1 (.in(and_5_out));
  and and_5 (and_5_out, register_1_q[1], not_8_out);
  not not_8 (not_8_out, and_3_out);
  not not_9 (not_9_out, register_1_q[1]);
  and and_6 (and_6_out, not_9_out, and_3_out);
  not not_10 (not_10_out, and_3_out);
  and and_7 (and_7_out, not_10_out, not_11_out);
  not not_11 (not_11_out, register_1_q[1]);
  LED #(.active("true")) led_2 (.in(and_8_out));
  and and_8 (and_8_out, not_7_out, not_12_out);
  not not_12 (not_12_out, and_4_out);
  not not_13 (not_13_out, not_7_out);
  and and_9 (and_9_out, not_13_out, and_4_out);
  not not_14 (not_14_out, and_4_out);
  and and_10 (and_10_out, not_14_out, not_15_out);
  not not_15 (not_15_out, not_7_out);
  LED #(.active("true")) led_3 (.in(and_6_out));
  LED #(.active("true")) led_4 (.in(and_9_out));
  LED #(.active("true")) LA (.in(and_7_out));
  LED #(.active("true")) LB (.in(and_10_out));
endmodule

module \售糖机Mealy型  (
);

  wire and_1_out, and_2_out, and_3_out, and_4_out, and_5_out, and_6_out, and_7_out, and_8_out, and_9_out,
       button_1_out, not_1_out, not_2_out, not_3_out, not_4_out, not_5_out, not_6_out, not_7_out, not_8_out,
       not_9_out, not_10_out, or_1_out, \五分_out , \十分_out ;
  wire [2:0] or_2_out, register_1_q;
  wire [3:0] counter_1_q;

  Button \u_十分  (.out(\十分_out ));
  Button \u_五分  (.out(\五分_out ));
  or or_1 (or_1_out, \五分_out , \十分_out );
  not not_1 (not_1_out, register_1_q[2]);
  not not_2 (not_2_out, register_1_q[1]);
  not not_3 (not_3_out, \十分_out );
  not not_4 (not_4_out, \五分_out );
  not not_5 (not_5_out, register_1_q[2]);
  not not_6 (not_6_out, register_1_q[1]);
  not not_7 (not_7_out, \十分_out );
  not not_8 (not_8_out, \五分_out );
  and and_1 (and_1_out, register_1_q[1], \十分_out );
  and and_2 (and_2_out, register_1_q[2], \五分_out );
  and and_3 (and_3_out, register_1_q[2], \十分_out );
  not not_9 (not_9_out, not_10_out);
  not not_10 (not_10_out, or_1_out);
  and and_4 (and_4_out, not_1_out, not_2_out, \十分_out );
  and and_5 (and_5_out, register_1_q[1], \五分_out );
  and and_6 (and_6_out, register_1_q[2], not_3_out, not_4_out);
  and and_7 (and_7_out, not_5_out, not_6_out, \五分_out );
  and and_8 (and_8_out, register_1_q[1], not_7_out, not_8_out);
  and and_9 (and_9_out, register_1_q[2], \十分_out );
  or or_2 (or_2_out[0], and_1_out, and_2_out, and_3_out);
  or or_3 (or_2_out[2], and_4_out, and_5_out, and_6_out);
  or or_4 (or_2_out[1], and_7_out, and_8_out, and_9_out);
  Counter #(.width(4), .max('hf), .ongoal("wrap"), .trigger("rising"), .behavior("old")) counter_1 (
    .Q(counter_1_q), .clk(register_1_q[0]), .clr(button_1_out));  // open: load, D, count, carry, preset
  Register #(.width(3), .trigger("rising"), .Select("low")) register_1 (
    .D(or_2_out), .Q(register_1_q), .clk(not_9_out), .clr(button_1_out));  // open: en
  Button button_1 (.out(button_1_out));
  Hex_Digit_Display hex_digit_display_1 (.value(counter_1_q));  // open: dp
endmodule

module \售糖机Moore型  (
  input  \十分 ,
  input  \五分 
);

  wire and_1_out, and_2_out, and_3_out, and_4_out, and_5_out, and_6_out, and_7_out, and_8_out, and_9_out,
       and_10_out, and_14_out, button_1_out, clock_1_out, nand_1_out, not_1_out, not_2_out, not_3_out,
       not_4_out, not_5_out, not_6_out, not_7_out, not_8_out, not_9_out, not_10_out, or_1_out, or_2_out,
       or_3_out, \售糖机控制器_1_a , \售糖机控制器_1_b , \售糖机控制器_1_c , \售糖机控制器_1_d , \售糖机控制器_1_e , \售糖机控制器_1_f ,
       \售糖机控制器_1_g ;
  wire [2:0] and_11_out, register_1_q;
  wire [3:0] counter_1_q;

  not not_1 (not_1_out, register_1_q[0]);
  and and_1 (and_1_out, register_1_q[1], not_1_out, \十分 );
  not not_2 (not_2_out, register_1_q[1]);
  and and_2 (and_2_out, not_2_out, \十分 );
  not not_3 (not_3_out, register_1_q[1]);
  and and_3 (and_3_out, not_3_out, register_1_q[0], \五分 );
  and and_4 (and_4_out, register_1_q[0], \十分 );
  not not_4 (not_4_out, register_1_q[0]);
  and and_5 (and_5_out, register_1_q[1], not_4_out, not_5_out);
  not not_5 (not_5_out, \十分 );
  and and_6 (and_6_out, register_1_q[2], \五分 );
  not not_6 (not_6_out, register_1_q[2]);
  and and_7 (and_7_out, not_6_out, not_7_out, \五分 );
  not not_7 (not_7_out, register_1_q[0]);
  not not_8 (not_8_out, register_1_q[1]);
  and and_8 (and_8_out, not_8_out, register_1_q[0], not_9_out);
  not not_9 (not_9_out, \五分 );
  and and_9 (and_9_out, register_1_q[1], \五分 );
  and and_10 (and_10_out, register_1_q[2], not_10_out);
  not not_10 (not_10_out, \五分 );
  nand nand_1 (nand_1_out, \十分 , \五分 );
  or or_1 (or_1_out, and_2_out, and_3_out, and_4_out, and_5_out, and_6_out);
  or or_2 (or_2_out, and_7_out, and_8_out, and_9_out, and_10_out);
  Clock #(.highDuration(1), .lowDuration(1)) clock_1 (.out(clock_1_out));
  and and_11 (and_11_out[0], or_2_out, nand_1_out);
  and and_12 (and_11_out[1], or_1_out, nand_1_out);
  and and_13 (and_11_out[2], nand_1_out, and_1_out);
  Register #(.width(3), .trigger("rising"), .Select("low")) register_1 (
    .D(and_11_out), .en(nand_1_out), .Q(register_1_q), .clk(clock_1_out), .clr(button_1_out));
  Button button_1 (.out(button_1_out));
  \售糖机控制器  \u_售糖机控制器_1  (
    .S2(register_1_q[2]), .S1(register_1_q[1]), .S0(register_1_q[0]), .a(\售糖机控制器_1_a ), .b(\售糖机控制器_1_b ),
    .c(\售糖机控制器_1_c ), .d(\售糖机控制器_1_d ), .e(\售糖机控制器_1_e ), .f(\售糖机控制器_1_f ), .g(\售糖机控制器_1_g ));
  Hex_Digit_Display hex_digit_display_1 (.value(counter_1_q));  // open: dp
  and and_14 (and_14_out, register_1_q[1], register_1_q[0]);
  _7_Segment_Display #(.active("true")) u_7_segment_display_1 (
    .b(register_1_q[1]), .c(register_1_q[1]));  // open: g, f, a, e, d, dp
  _7_Segment_Display #(.active("true")) u_7_segment_display_2 (
    .g(\售糖机控制器_1_g ), .f(\售糖机控制器_1_f ), .a(\售糖机控制器_1_a ), .b(\售糖机控制器_1_b ), .e(\售糖机控制器_1_e ),
    .d(\售糖机控制器_1_d ), .c(\售糖机控制器_1_c ));  // open: dp
  or or_3 (or_3_out, register_1_q[2], and_14_out);
  // Probe on or_3_out
  Counter #(.width(4), .max('hf), .ongoal("wrap"), .trigger("rising"), .behavior("old")) counter_1 (
    .Q(counter_1_q), .clk(or_3_out), .clr(button_1_out));  // open: load, D, count, carry, preset
endmodule

module \售糖机控制器  (
  input  S2,
  input  S1,
  input  S0,
  output a,
  output b,
  output c,
  output d,
  output e,
  output f,
  output g
);

  wire and_1_out, and_3_out, and_4_out, and_6_out, and_7_out, and_8_out, not_1_out, not_2_out, not_3_out,
       not_4_out, not_5_out, not_6_out, not_7_out, not_8_out, not_9_out, not_10_out, not_11_out, not_12_out,
       not_13_out, not_14_out, not_15_out, not_16_out, not_17_out, not_18_out, not_19_out;

  not not_1 (not_1_out, S1);
  not not_2 (not_2_out, S0);
  not not_3 (not_3_out, S2);
  not not_4 (not_4_out, S0);
  not not_5 (not_5_out, S1);
  not not_6 (not_6_out, S0);
  not not_7 (not_7_out, S1);
  not not_8 (not_8_out, S0);
  not not_9 (not_9_out, S2);
  not not_10 (not_10_out, S0);
  not not_11 (not_11_out, S1);
  not not_12 (not_12_out, S0);
  not not_13 (not_13_out, S2);
  not not_14 (not_14_out, S1);
  not not_15 (not_15_out, S0);
  not not_16 (not_16_out, S2);
  and and_1 (and_1_out, not_1_out, not_2_out);
  and and_2 (b, not_3_out, not_4_out);
  not not_17 (not_17_out, S2);
  and and_3 (and_3_out, not_5_out, not_6_out);
  not not_18 (not_18_out, S2);
  and and_4 (and_4_out, not_7_out, not_8_out);
  and and_5 (e, not_9_out, not_10_out);
  not not_19 (not_19_out, S2);
  and and_6 (and_6_out, not_11_out, not_12_out);
  and and_7 (and_7_out, not_13_out, S0);
  and and_8 (and_8_out, S2, not_14_out, not_15_out);
  or or_1 (a, not_16_out, and_1_out);
  or or_2 (c, not_17_out, and_3_out);
  or or_3 (d, not_18_out, and_4_out);
  or or_4 (f, not_19_out, and_6_out);
  or or_5 (g, and_7_out, and_8_out);
endmodule

module \存储器讨论问题1  (
  input  [15:0] \地址 ,
  input  [7:0] \数据写入 ,
  input  in_3,
  input  in_4,
  output [7:0] \数据读取 
);

  wire and_1_out, and_2_out, and_3_out, and_4_out, and_5_out, and_6_out, and_7_out, and_8_out, clock_1_out,
       decoder_1_out0, decoder_1_out1, decoder_1_out7, not_1_out, not_2_out, not_3_out, not_4_out;

  Decoder #(.select(3), .tristate("false"), .disabled("Z"), .enable("true")) decoder_1 (
    .out0(decoder_1_out0), .out1(decoder_1_out1), .out7(decoder_1_out7), .sel(\地址 [15:13]));  // open: out2, out3, out4, out5, out6, en
  not not_1 (not_1_out, \地址 [11]);
  not not_2 (not_2_out, \地址 [12]);
  not not_3 (not_3_out, \地址 [11]);
  not not_4 (not_4_out, \地址 [12]);
  and and_1 (and_1_out, not_1_out, not_2_out);
  and and_2 (and_2_out, not_3_out, \地址 [12]);
  and and_3 (and_3_out, \地址 [11], not_4_out);
  and and_4 (and_4_out, \地址 [11], \地址 [12]);
  Clock #(.highDuration(1), .lowDuration(1)) clock_1 (.out(clock_1_out));
  ROM #(.addrWidth(11), .dataWidth(8), .Select("high")) rom_1 (.addr(\地址 [10:0]), .data(\数据读取 ), .sel(and_5_out));
  ROM #(.addrWidth(11), .dataWidth(8), .Select("high")) rom_2 (.addr(\地址 [10:0]), .data(\数据读取 ), .sel(and_6_out));
  RAM #(.addrWidth(11), .dataWidth(8), .bus("separate"), .Select("high")) ram_1 (
    .addr(\地址 [10:0]), .din(\数据写入 ), .data(\数据读取 ), .str(in_3), .sel(and_7_out), .clk(clock_1_out), .ld(in_4));  // open: clr
  RAM #(.addrWidth(11), .dataWidth(8), .bus("separate"), .Select("high")) ram_2 (
    .addr(\地址 [10:0]), .din(\数据写入 ), .data(\数据读取 ), .str(in_3), .sel(and_8_out), .clk(clock_1_out), .ld(in_4));  // open: clr
  RAM #(.addrWidth(13), .dataWidth(8), .bus("separate"), .Select("high")) ram_3 (
    .addr(\地址 [12:0]), .din(\数据写入 ), .data(\数据读取 ), .str(in_3), .sel(decoder_1_out1), .clk(clock_1_out),
    .ld(in_4));  // open: clr
  RAM #(.addrWidth(13), .dataWidth(8), .bus("separate"), .Select("high")) ram_4 (
    .addr(\地址 [12:0]), .din(\数据写入 ), .data(\数据读取 ), .str(in_3), .sel(decoder_1_out0), .clk(clock_1_out),
    .ld(in_4));  // open: clr
  and and_5 (and_5_out, decoder_1_out7, and_4_out);
  and and_6 (and_6_out, decoder_1_out7, and_3_out);
  and and_7 (and_7_out, decoder_1_out7, and_2_out);
  and and_8 (and_8_out, decoder_1_out7, and_1_out);
endmodule

module \存储器讨论问题2  (
  input  in_1,
  input  in_2,
  input  [25:0] \地址 ,
  input  [15:0] \数据写入 ,
  output [15:0] \数据读取 
);

  wire clock_1_out, decoder_1_out0, decoder_1_out1, decoder_1_out2, decoder_1_out3;

  // Probe on \数据写入 
  // Probe on \地址 
  Decoder #(.select(2), .tristate("false"), .disabled("Z"), .enable("true")) decoder_1 (
    .out0(decoder_1_out0), .out1(decoder_1_out1), .out2(decoder_1_out2), .out3(decoder_1_out3),
    .sel(\地址 [1:0]));  // open: en
  Clock #(.highDuration(1), .lowDuration(1)) clock_1 (.out(clock_1_out));
  RAM #(.addrWidth(24), .dataWidth(8), .bus("separate"), .Select("high")) ram_1 (
    .addr(\地址 [25:2]), .din(\数据写入 [15:8]), .data(\数据读取 [15:8]), .str(in_1), .sel(decoder_1_out0),
    .clk(clock_1_out), .ld(in_2));  // open: clr
  RAM #(.addrWidth(24), .dataWidth(8), .bus("separate"), .Select("high")) ram_2 (
    .addr(\地址 [25:2]), .din(\数据写入 [7:0]), .data(\数据读取 [7:0]), .str(in_1), .sel(decoder_1_out0),
    .clk(clock_1_out), .ld(in_2));  // open: clr
  RAM #(.addrWidth(24), .dataWidth(8), .bus("separate"), .Select("high")) ram_3 (
    .addr(\地址 [25:2]), .din(\数据写入 [15:8]), .data(\数据读取 [7:0]), .str(in_1), .sel(decoder_1_out1),
    .clk(clock_1_out), .ld(in_2));  // open: clr
  RAM #(.addrWidth(24), .dataWidth(8), .bus("separate"), .Select("high")) ram_4 (
    .addr(\地址 [25:2]), .din(\数据写入 [7:0]), .data(\数据读取 [15:8]), .str(in_1), .sel(decoder_1_out1),
    .clk(clock_1_out), .ld(in_2));  // open: clr
  RAM #(.addrWidth(24), .dataWidth(8), .bus("separate"), .Select("high")) ram_5 (
    .addr(\地址 [25:2]), .din(\数据写入 [15:8]), .data(\数据读取 [7:0]), .str(in_1), .sel(decoder_1_out2),
    .clk(clock_1_out), .ld(in_2));  // open: clr
  RAM #(.addrWidth(24), .dataWidth(8), .bus("separate"), .Select("high")) ram_6 (
    .addr(\地址 [25:2]), .din(\数据写入 [7:0]), .data(\数据读取 [15:8]), .str(in_1), .sel(decoder_1_out2),
    .clk(clock_1_out), .ld(in_2));  // open: clr
  RAM #(.addrWidth(24), .dataWidth(8), .bus("separate"), .Select("high")) ram_7 (
    .addr(\地址 [25:2]), .din(\数据写入 [15:8]), .data(\数据读取 [7:0]), .str(in_1), .sel(decoder_1_out3),
    .clk(clock_1_out), .ld(in_2));  // open: clr
  RAM #(.addrWidth(24), .dataWidth(8), .bus("separate"), .Select("high")) ram_8 (
    .addr(\地址 [25:2]), .din(\数据写入 [7:0]), .data(\数据读取 [15:8]), .str(in_1), .sel(decoder_1_out3),
    .clk(clock_1_out), .ld(in_2));  // open: clr
  // Probe on \数据读取 
endmodule

module \实验2_乘法器  (
  input  reset,
  input  [7:0] A,
  input  [7:0] B,
  input  [7:0] in_4,
  output [15:0] out
);

  wire B0, B_t, clock, comparator_1_eq, Done, LA, LB, LP, SA, SB, Start_out;
  wire [7:0] B_q, multiplexer_2_out, shifter_2_out;
  wire [15:0] A_q, adder_1_out, bit_extender_1_out, multiplexer_1_out, shifter_1_out;

  // Probe on bit_extender_1_out
  Clock #(.highDuration(1), .lowDuration(1)) u_clock (.out(clock));
  Multiplexer #(.select(1), .width(16), .disabled("Z"), .enable("true")) multiplexer_1 (
    .in0(bit_extender_1_out), .in1(shifter_1_out), .out(multiplexer_1_out), .sel(SA));  // open: en
  Register #(.width(16), .trigger("rising"), .Select("low")) u_A (
    .D(multiplexer_1_out), .en(LA), .Q(A_q), .clk(clock), .clr(reset));
  Button Start (.out(Start_out));
  Adder #(.width(16)) adder_1 (.a(out), .b(A_q), .out(adder_1_out));  // open: cin, cout
  // Probe on out
  assign bit_extender_1_out = {{8{1'b0}}, A};  // Bit_Extender bit_extender_1
  Shifter #(.width(16), .shift("ll")) shifter_1 (.in(A_q), .\dist (4'b0001), .out(shifter_1_out));
  Register #(.width(16), .trigger("rising"), .Select("low")) P (
    .D(adder_1_out), .en(LP), .Q(out), .clk(clock), .clr(reset));
  \乘法器FSM  \u_控制器  (
    .start(Start_out), .B(B_t), .B0(B0), .clock(clock), .reset(reset), .LA(LA), .SA(SA), .LB(LB), .SB(SB),
    .LP(LP), .Done(Done));
  Multiplexer #(.select(1), .width(8), .disabled("Z"), .enable("true")) multiplexer_2 (
    .in0(B), .in1(shifter_2_out), .out(multiplexer_2_out), .sel(SB));  // open: en
  Register #(.width(8), .trigger("rising"), .Select("low")) u_B (
    .D(multiplexer_2_out), .en(LB), .Q(B_q), .clk(clock), .clr(reset));
  // Probe on B
  BitSelector #(.width(8), .group(1)) bitselector_1 (.in(B_q), .out(B0), .sel(3'b000));
  not not_1 (B_t, comparator_1_eq);
  Comparator #(.width(8), .mode("twosComplement")) comparator_1 (
    .a(B_q), .b(in_4), .eq(comparator_1_eq));  // open: gt, lt
  Shifter #(.width(8), .shift("lr")) shifter_2 (.in(B_q), .\dist (3'b001), .out(shifter_2_out));

  // Other names for the same wires on the sheet: X[7:0] = A; Y[7:0] = B
endmodule

module \乘法器FSM  (
  input  start,
  input  B,
  input  B0,
  input  clock,
  input  reset,
  output LA,
  output SA,
  output LB,
  output SB,
  output LP,
  output Done
);

  wire and_1_out, and_2_out, and_3_out, and_4_out, and_5_out, and_6_out, and_7_out, and_8_out, and_9_out,
       and_10_out, not_1_out, not_2_out, not_3_out, not_4_out, not_5_out, not_6_out, not_7_out, not_8_out,
       not_9_out, not_10_out, not_11_out, not_12_out, not_13_out;
  wire [0:0] register_1_q;
  wire [2:0] or_3_out;

  not not_1 (not_1_out, SA);
  not not_2 (not_2_out, B);
  not not_3 (not_3_out, Done);
  not not_4 (not_4_out, SA);
  not not_5 (not_5_out, Done);
  not not_6 (not_6_out, SA);
  not not_7 (not_7_out, Done);
  not not_8 (not_8_out, register_1_q[0]);
  not not_9 (not_9_out, Done);
  and and_1 (and_1_out, not_1_out, register_1_q[0], not_2_out);
  and and_2 (and_2_out, not_3_out, not_4_out, register_1_q[0], B0);
  and and_3 (and_3_out, not_5_out, not_6_out, register_1_q[0], B);
  and and_4 (and_4_out, Done, SA);
  and and_5 (and_5_out, not_7_out, not_8_out, start);
  and and_6 (and_6_out, register_1_q[0], B0);
  and and_7 (and_7_out, not_9_out, SA);
  and and_8 (and_8_out, Done, register_1_q[0]);
  or or_1 (or_3_out[2], and_1_out, Done);
  or or_2 (or_3_out[1], and_2_out, and_3_out, and_4_out);
  or or_3 (or_3_out[0], and_5_out, and_6_out, and_7_out, and_8_out);
  Register #(.width(3), .trigger("rising"), .Select("low")) register_1 (
    .D(or_3_out), .Q({Done, SA, register_1_q[0]}), .clk(clock), .clr(reset));  // open: en
  not not_10 (not_10_out, Done);
  and and_9 (and_9_out, not_10_out, not_11_out);
  not not_11 (not_11_out, register_1_q[0]);
  not not_12 (not_12_out, Done);
  and and_10 (and_10_out, not_12_out, not_13_out);
  not not_13 (not_13_out, register_1_q[0]);
  and and_11 (LP, SA, register_1_q[0]);
  or or_4 (LA, and_9_out, SA);
  or or_5 (LB, and_10_out, SA);

  assign SB = SA;
endmodule

// ALU
module \算术逻辑运算单元ALU  (
  input  [31:0] X,
  input  [31:0] Y,
  input  [2:0] AluOP,
  output \结果是否为0 ,
  output [31:0] Result
);

  wire comparator_1_lt;
  wire [24:0] \运算指示 ;
  wire [31:0] adder_1_out, and_1_out, and_2_out, bit_extender_1_out, not_1_out, not_2_out, or_1_out,
       or_2_out, subtractor_1_out, subtractor_2_out;

  // Probe on X
  // Probe on X
  // Probe on Y
  // Probe on Y
  assign not_1_out = ~Y;  // NOT_Gate not_1, 32 bits wide
  assign not_2_out = ~Y;  // NOT_Gate not_2, 32 bits wide
  // Probe on AluOP
  assign and_1_out = X & Y;  // AND_Gate and_1, 32 bits wide
  assign or_1_out = X | Y;  // OR_Gate or_1, 32 bits wide
  Adder #(.width(32)) adder_1 (.a(X), .b(Y), .out(adder_1_out));  // open: cin, cout
  assign and_2_out = X & not_1_out;  // AND_Gate and_2, 32 bits wide
  assign or_2_out = X | not_2_out;  // OR_Gate or_2, 32 bits wide
  Subtractor #(.width(32)) subtractor_1 (.a(X), .b(Y), .out(subtractor_1_out));  // open: bin, bout
  Subtractor #(.width(32)) subtractor_2 (.a(X), .b(Y), .out(subtractor_2_out));  // open: bin, bout
  // Probe on Result
  // Probe on Result
  Comparator #(.width(32), .mode("twosComplement")) comparator_1 (
    .a(subtractor_2_out), .b({32{1'b0}}), .lt(comparator_1_lt));  // open: gt, eq
  DotMatrix #(.inputtype("column"), .matrixcols(5), .matrixrows(5), .persist(0), .dotshape("square")) dotmatrix_1 (
    .col0(\运算指示 [24:20]), .col1(\运算指示 [19:15]), .col2(\运算指示 [14:10]), .col3(\运算指示 [9:5]), .col4(\运算指示 [4:0]));
  assign bit_extender_1_out = {{31{1'b0}}, comparator_1_lt};  // Bit_Extender bit_extender_1
  Multiplexer #(.select(3), .width(25), .disabled("Z"), .enable("false")) multiplexer_1 (
    .in0(25'h124081), .in1(25'h1020490), .in2(25'h427c84), .in3({25{1'b0}}), .in4(25'h124091),
    .in5(25'h1020490), .in6(25'h421084), .in7(25'h402811), .out(\运算指示 ), .sel(AluOP));
  Multiplexer #(.select(3), .width(32), .disabled("Z"), .enable("true")) multiplexer_2 (
    .in0(and_1_out), .in1(or_1_out), .in2(adder_1_out), .in3(32'h1), .in4(and_2_out), .in5(or_2_out),
    .in6(subtractor_1_out), .in7(bit_extender_1_out), .out(Result), .sel(AluOP));  // open: en
  Comparator #(.width(32), .mode("twosComplement")) comparator_2 (
    .a(Result), .b({32{1'b0}}), .eq(\结果是否为0 ));  // open: gt, lt

  // Other names for the same wires on the sheet: S[2:0] = AluOP; Zero = \结果是否为0 

  // Notes on the sheet:
  //   AluOP: pull=down
  //   X: pull=down
  //   Y: pull=down
  //   不要改变此引脚区域内容，也不要改变ALU封装形式
  //   请在下方利用上方输入输出引脚的隧道信号构建ALU电路，ctrl+d复制选择部件
  //   输入引脚
  //   探测区域
  //   输出引脚
  //   功能说明：
  //   000：X AND Y      100：X AND Y'
  //   001：X OR Y        101：X OR Y'  
  //   010：X + Y           110：X - Y  
  //   011：未使用         111：SLT  
endmodule

module \ALU自动测试  (
  output [7:0] TEST_num
);

  wire ADD, AND, and_1_out, AND_prime, CLK, comparator_2_eq, HALT, Halt_t, multiplexer_1_out, nHalt, NotEQ,
       OR, OR_prime, priority_encoder_1_gs, Rok, SLT, SUB, X___Y, X___Y_t, X_AND_Y, X_AND_Y_prime, X_OR_Y,
       X_OR_Y_prime, X_Y, xnor_1_out, Zero, Zero_Standard, \悬空检测 ;
  wire [2:0] ALUOP;
  wire [3:0] \个位 , \十位 , \百位 ;
  wire [7:0] adder_1_out, \单项评分_1_总条数 , \单项评分_1_扣分 , \单项评分_1_正确条数 , \单项评分_2_总条数 , \单项评分_2_扣分 , \单项评分_2_正确条数 ,
       \单项评分_3_总条数 , \单项评分_3_扣分 , \单项评分_3_正确条数 , \单项评分_4_总条数 , \单项评分_4_扣分 , \单项评分_4_正确条数 , \单项评分_5_总条数 ,
       \单项评分_5_扣分 , \单项评分_5_正确条数 , \单项评分_6_总条数 , \单项评分_6_扣分 , \单项评分_6_正确条数 , \单项评分_7_总条数 , \单项评分_7_扣分 ,
       \单项评分_7_正确条数 , \单项评分_8_扣分 , \总项评分_1_总分 ;
  wire [9:0] counter_1_q;
  wire [31:0] bit_extender_1_out, R, R_Standard, X, Y;

  Register #(.width(8), .trigger("rising"), .Select("low")) register_1 (
    .D(adder_1_out), .en(nHalt), .Q(TEST_num), .clk(CLK));  // open: clr
  Clock #(.highDuration(1), .lowDuration(1)) clock_1 (.out(CLK));
  \单项评分  \u_单项评分_1  (
    .ALUOP(AND), .\扣分 (\单项评分_1_扣分 ), .\正确条数 (\单项评分_1_正确条数 ), .Rok(Rok), .nHalt(nHalt), .Right(X_AND_Y),
    .CLK(CLK), .\总条数 (\单项评分_1_总条数 ), .NotEQ(NotEQ));
  // Probe on \单项评分_1_总条数 
  // Probe on \单项评分_1_正确条数 
  // Probe on \单项评分_1_扣分 
  Adder #(.width(8)) adder_1 (.a(8'h1), .b(TEST_num), .out(adder_1_out));  // open: cin, cout
  not not_1 (nHalt, Halt_t);
  Comparator #(.width(3), .mode("twosComplement")) comparator_1 (.a(ALUOP), .b(3'b011), .eq(Halt_t));  // open: gt, lt
  Counter #(.width(10), .max('h3ff), .ongoal("wrap"), .trigger("rising"), .behavior("old")) counter_1 (
    .count(NotEQ), .Q(counter_1_q), .clk(CLK), .clr(Halt_t));  // open: load, D, carry, preset
  and and_1 (and_1_out, ~Halt_t, NotEQ);  // AND_Gate
  \单项评分  \u_单项评分_2  (
    .ALUOP(OR), .\扣分 (\单项评分_2_扣分 ), .\正确条数 (\单项评分_2_正确条数 ), .Rok(Rok), .nHalt(nHalt), .Right(X_OR_Y),
    .CLK(CLK), .\总条数 (\单项评分_2_总条数 ), .NotEQ(NotEQ));
  // Probe on \单项评分_2_总条数 
  // Probe on \单项评分_2_正确条数 
  // Probe on \单项评分_2_扣分 
  \总项评分  \u_总项评分_1  (
    .in_1(\单项评分_1_扣分 ), .in_2(\单项评分_2_扣分 ), .in_3(\单项评分_3_扣分 ), .in_4(\单项评分_4_扣分 ), .in_5(\单项评分_5_扣分 ),
    .in_6(\单项评分_6_扣分 ), .in_8(\单项评分_7_扣分 ), .in_9(\单项评分_8_扣分 ), .\总分 (\总项评分_1_总分 ), .\百位 (\百位 ), .\十位 (\十位 ),
    .\个位 (\个位 ), .\Zero悬空扣分 (\悬空检测 ));
  trace trace_1 (.in_1(TEST_num), .X(X), .Y(Y), .AluOP(ALUOP), .R(R_Standard), .Zero(Zero_Standard));
  \单项评分  \u_单项评分_3  (
    .ALUOP(ADD), .\扣分 (\单项评分_3_扣分 ), .\正确条数 (\单项评分_3_正确条数 ), .Rok(Rok), .nHalt(nHalt), .Right(X___Y),
    .CLK(CLK), .\总条数 (\单项评分_3_总条数 ), .NotEQ(NotEQ));
  // Probe on \单项评分_3_总条数 
  // Probe on \单项评分_3_正确条数 
  // Probe on \单项评分_3_扣分 
  RAM #(.addrWidth(10), .dataWidth(32), .bus("separate"), .Select("high")) ram_1 (
    .addr(counter_1_q), .din(X), .str(and_1_out), .clk(CLK));  // open: data, sel, ld, clr
  \单项评分  \u_单项评分_4  (
    .ALUOP(AND_prime), .\扣分 (\单项评分_4_扣分 ), .\正确条数 (\单项评分_4_正确条数 ), .Rok(Rok), .nHalt(nHalt),
    .Right(X_AND_Y_prime), .CLK(CLK), .\总条数 (\单项评分_4_总条数 ), .NotEQ(NotEQ));
  // Probe on \单项评分_4_总条数 
  // Probe on \单项评分_4_正确条数 
  // Probe on \单项评分_4_扣分 
  \单项评分  \u_单项评分_5  (
    .ALUOP(OR_prime), .\扣分 (\单项评分_5_扣分 ), .\正确条数 (\单项评分_5_正确条数 ), .Rok(Rok), .nHalt(nHalt),
    .Right(X_OR_Y_prime), .CLK(CLK), .\总条数 (\单项评分_5_总条数 ), .NotEQ(NotEQ));
  // Probe on \单项评分_5_总条数 
  // Probe on \单项评分_5_正确条数 
  // Probe on \单项评分_5_扣分 
  // Probe on \总项评分_1_总分 
  \算术逻辑运算单元ALU  \u_算术逻辑运算单元alu_1  (.AluOP(ALUOP), .X(X), .Result(R), .Y(Y), .\结果是否为0 (Zero));
  RAM #(.addrWidth(10), .dataWidth(32), .bus("separate"), .Select("high")) ram_2 (
    .addr(counter_1_q), .din(Y), .str(and_1_out), .clk(CLK));  // open: data, sel, ld, clr
  assign bit_extender_1_out = {{29{1'b0}}, ALUOP};  // Bit_Extender bit_extender_1
  \单项评分  \u_单项评分_6  (
    .ALUOP(SUB), .\扣分 (\单项评分_6_扣分 ), .\正确条数 (\单项评分_6_正确条数 ), .Rok(Rok), .nHalt(nHalt), .Right(X___Y_t),
    .CLK(CLK), .\总条数 (\单项评分_6_总条数 ), .NotEQ(NotEQ));
  // Probe on \单项评分_6_总条数 
  // Probe on \单项评分_7_总条数 
  // Probe on \单项评分_6_正确条数 
  // Probe on \单项评分_6_扣分 
  \单项评分  \u_单项评分_7  (
    .ALUOP(SLT), .\扣分 (\单项评分_7_扣分 ), .\正确条数 (\单项评分_7_正确条数 ), .Rok(Rok), .nHalt(nHalt), .Right(X_Y),
    .CLK(CLK), .\总条数 (\单项评分_7_总条数 ), .NotEQ(NotEQ));
  // Probe on \单项评分_7_正确条数 
  // Probe on \单项评分_7_扣分 
  // Probe on ALUOP
  \单项评分  \u_单项评分_8  (
    .ALUOP(1'b0), .\扣分 (\单项评分_8_扣分 ), .Rok(Rok), .nHalt(nHalt), .CLK(CLK), .NotEQ(NotEQ));  // open: 正确条数, Right, 总条数
  RAM #(.addrWidth(10), .dataWidth(32), .bus("separate"), .Select("high")) ram_3 (
    .addr(counter_1_q), .din(bit_extender_1_out), .str(and_1_out), .clk(CLK));  // open: data, sel, ld, clr
  Decoder #(.select(3), .tristate("false"), .disabled("Z"), .enable("false")) decoder_1 (
    .out0(AND), .out1(OR), .out2(ADD), .out3(HALT), .out4(AND_prime), .out5(OR_prime), .out6(SUB),
    .out7(SLT), .sel(ALUOP));
  Multiplexer #(.select(1), .width(1), .disabled("Z"), .enable("false")) multiplexer_1 (
    .in0(1'b1), .in1(1'b1), .out(multiplexer_1_out), .sel(Zero));
  xnor xnor_1 (xnor_1_out, Zero_Standard, Zero);
  Comparator #(.width(32), .mode("twosComplement")) comparator_2 (
    .a(R_Standard), .b(R), .eq(comparator_2_eq));  // open: gt, lt
  LED #(.active("false")) led_1 (.in(X_AND_Y));
  LED #(.active("false")) led_2 (.in(X_OR_Y));
  LED #(.active("false")) led_3 (.in(X___Y));
  LED #(.active("false")) led_4 (.in(X_AND_Y_prime));
  LED #(.active("false")) led_5 (.in(X_OR_Y_prime));
  LED #(.active("false")) led_6 (.in(X___Y_t));
  LED #(.active("false")) led_7 (.in(X_Y));
  LED #(.active("true")) led_8 (.in(NotEQ));
  Priority_Encoder #(.select(1), .disabled("Z")) priority_encoder_1 (
    .in0(multiplexer_1_out), .in1(multiplexer_1_out), .gs(priority_encoder_1_gs));  // open: out, en_out, en_in
  not not_2 (\悬空检测 , priority_encoder_1_gs);
  nand nand_1 (NotEQ, xnor_1_out, Rok);
  Priority_Encoder #(.select(1), .disabled("Z")) priority_encoder_2 (
    .in0(comparator_2_eq), .in1(comparator_2_eq), .gs(Rok));  // open: out, en_out, en_in
  Hex_Digit_Display hex_digit_display_1 (.value(\百位 ));  // open: dp
  Hex_Digit_Display hex_digit_display_2 (.value(\十位 ));  // open: dp
  Hex_Digit_Display hex_digit_display_3 (.value(\个位 ));  // open: dp

  // Notes on the sheet:
  //   X 错误记录
  //   Y 错误记录
  //   ALUOP 错误记录
  //   运算故障指示
  //   红色异常
  //   成绩
endmodule

module trace (
  input  [7:0] in_1,
  output [31:0] X,
  output [31:0] Y,
  output [2:0] AluOP,
  output [31:0] R,
  output Zero
);

  ROM #(.addrWidth(8), .dataWidth(32), .Select("high")) rom_1 (.addr(in_1), .data(X));
  ROM #(.addrWidth(8), .dataWidth(32), .Select("high")) rom_2 (.addr(in_1), .data(Y));
  ROM #(.addrWidth(8), .dataWidth(3), .Select("high")) rom_3 (.addr(in_1), .data(AluOP));
  ROM #(.addrWidth(8), .dataWidth(32), .Select("high")) rom_4 (.addr(in_1), .data(R));
  ROM #(.addrWidth(8), .dataWidth(1), .Select("high")) rom_5 (.addr(in_1), .data(Zero));

  // Notes on the sheet:
  //   X trace
  //   contents of rom_1 (hex, n*v repeats v):
  //   1 1 1 0 11111111 0 0 0 10b67f2
  //   Y trace
  //   contents of rom_2 (hex, n*v repeats v):
  //   1 0 1 4*0 1 2f5a0df4
  //   ALU OP Trace
  //   contents of rom_3 (hex, n*v repeats v):
  //   0 1 2 0 4 5 6 7 2
  //   Result
  //   contents of rom_4 (hex, n*v repeats v):
  //   1 1 2 0 11111111 ffffffff 0 1 306575e6
  //   Zero Flag
  //   contents of rom_5 (hex, n*v repeats v):
  //   0 0 0 1 0 0 1 0 0 247*1
endmodule

module \单项评分  (
  input  ALUOP,
  input  NotEQ,
  input  Rok,
  input  nHalt,
  input  CLK,
  output [7:0] \扣分 ,
  output [7:0] \正确条数 ,
  output Right,
  output [7:0] \总条数 
);

  wire and_1_out, and_2_out, and_3_out, and_4_out, comparator_1_eq, not_1_out, not_2_out, not_3_out,
       undriven, undriven_2, undriven_3, undriven_4;
  wire [7:0] counter_1_q, counter_2_q, multiplexer_1_out;

  not not_1 (not_1_out, NotEQ);
  and and_1 (and_1_out, undriven, undriven_2, undriven_4);
  and and_2 (and_2_out, undriven, undriven_4);
  and and_3 (and_3_out, ALUOP, not_1_out, Rok, nHalt);
  and and_4 (and_4_out, ALUOP, nHalt);
  Counter #(.width(8), .max('hff), .ongoal("wrap"), .trigger("rising"), .behavior("old")) counter_1 (
    .count(and_1_out), .Q(counter_1_q), .clk(undriven_3));  // open: load, D, carry, clr, preset
  Counter #(.width(8), .max('hff), .ongoal("wrap"), .trigger("rising"), .behavior("old")) counter_2 (
    .count(and_2_out), .Q(counter_2_q));  // open: load, D, carry, clk, clr, preset
  Counter #(.width(8), .max('hff), .ongoal("wrap"), .trigger("rising"), .behavior("old")) counter_3 (
    .count(and_3_out), .Q(\正确条数 ), .clk(CLK));  // open: load, D, carry, clr, preset
  Counter #(.width(8), .max('hff), .ongoal("wrap"), .trigger("rising"), .behavior("old")) counter_4 (
    .count(and_4_out), .Q(\总条数 ), .clk(CLK));  // open: load, D, carry, clr, preset
  Comparator #(.width(8), .mode("twosComplement")) comparator_1 (
    .a(counter_1_q), .b(counter_2_q), .eq(comparator_1_eq));  // open: gt, lt
  Comparator #(.width(8), .mode("twosComplement")) comparator_2 (.a(\正确条数 ), .b(\总条数 ), .eq(Right));  // open: gt, lt
  Multiplexer #(.select(1), .width(8), .disabled("Z"), .enable("false")) multiplexer_1 (
    .in0({8{1'b0}}), .in1(8'h5), .out(multiplexer_1_out), .sel(not_2_out));
  not not_2 (not_2_out, comparator_1_eq);
  not not_3 (not_3_out, Right);
  Multiplexer #(.select(1), .width(8), .disabled("Z"), .enable("false")) multiplexer_2 (
    .in0({8{1'b0}}), .in1(8'h5), .out(\扣分 ), .sel(not_3_out));

  // Notes on the sheet:
  //   ALUOP
  //   Rok
  //   ~Halt
  //   CLK
  //   Duplicated
  //   总条数
  //   正确条数
  //   扣分
  //   Right？
endmodule

module \总项评分  (
  input  [7:0] in_1,
  input  [7:0] in_2,
  input  [7:0] in_3,
  input  [7:0] in_4,
  input  [7:0] in_5,
  input  [7:0] in_6,
  input  \Zero悬空扣分 ,
  input  [7:0] in_8,
  input  [7:0] in_9,
  output [7:0] \总分 ,
  output [3:0] \百位 ,
  output [3:0] \十位 ,
  output [3:0] \个位 
);

  wire [7:0] adder_1_out, adder_2_out, adder_3_out, adder_4_out, adder_5_out, adder_6_out, adder_7_out,
       divider_1_out, subtractor_1_out, subtractor_2_out;
  wire [7:4] divider_1_rem, divider_2_out, divider_2_rem;

  Adder #(.width(8)) adder_1 (.a(in_1), .b(in_2), .out(adder_1_out));  // open: cin, cout
  Adder #(.width(8)) adder_2 (.a(in_3), .b(in_4), .out(adder_2_out));  // open: cin, cout
  Adder #(.width(8)) adder_3 (.a(in_5), .b(in_6), .out(adder_3_out));  // open: cin, cout
  Adder #(.width(8)) adder_4 (.a(in_8), .b(in_9), .out(adder_4_out));  // open: cin, cout
  Adder #(.width(8)) adder_5 (.a(adder_1_out), .b(adder_2_out), .out(adder_5_out));  // open: cin, cout
  Adder #(.width(8)) adder_6 (.a(adder_3_out), .b(adder_4_out), .out(adder_6_out));  // open: cin, cout
  Adder #(.width(8)) adder_7 (.a(adder_5_out), .b(adder_6_out), .out(adder_7_out));  // open: cin, cout
  Subtractor #(.width(8)) subtractor_1 (.a(8'h64), .b(adder_7_out), .out(subtractor_1_out));  // open: bin, bout
  Subtractor #(.width(8)) subtractor_2 (.a(subtractor_1_out), .b(8'h5), .out(subtractor_2_out));  // open: bin, bout
  Multiplexer #(.select(1), .width(8), .disabled("Z"), .enable("false")) multiplexer_1 (
    .in0(subtractor_1_out), .in1(subtractor_2_out), .out(\总分 ), .sel(\Zero悬空扣分 ));
  Divider #(.width(8)) divider_1 (.a(\总分 ), .b(8'ha), .out(divider_1_out), .rem({divider_1_rem, \个位 }));  // open: upper
  Divider #(.width(8)) divider_2 (
    .a(divider_1_out), .b(8'ha), .out({divider_2_out, \百位 }), .rem({divider_2_rem, \十位 }));  // open: upper
endmodule

module \_32位地址总线32位数据总线RAM存储器  (
  input  CS,
  input  Store,
  input  CLK,
  input  [31:0] Address_Bus,
  input  [31:0] Data_Bus_In,
  input  Load,
  input  Clear,
  output [31:0] Data_Bus_Out
);

  wire and_1_out, and_2_out, and_3_out, and_4_out, and_5_out, and_6_out, and_7_out, and_8_out, and_9_out,
       and_10_out, and_11_out, and_12_out, and_13_out, and_14_out, and_15_out, and_16_out, and_17_out,
       and_18_out, and_19_out, and_20_out, and_21_out, and_22_out, and_23_out, and_24_out, and_25_out,
       and_26_out, and_27_out, and_28_out, and_29_out, and_30_out, and_31_out, and_32_out, and_33_out,
       and_34_out, and_35_out, and_36_out, and_37_out, and_38_out, and_39_out, and_40_out, and_41_out,
       and_42_out, and_43_out, and_44_out, and_45_out, and_46_out, and_47_out, and_48_out, and_49_out,
       and_50_out, and_51_out, and_52_out, and_53_out, and_54_out, and_55_out, and_56_out, and_57_out,
       and_58_out, and_59_out, and_60_out, and_61_out, and_62_out, and_63_out, and_64_out, decoder_1_out0,
       decoder_1_out1, decoder_1_out2, decoder_1_out3, decoder_1_out4, decoder_1_out5, decoder_1_out6,
       decoder_1_out7, decoder_2_out0, decoder_2_out1, decoder_2_out2, decoder_2_out3, decoder_2_out4,
       decoder_2_out5, decoder_2_out6, decoder_2_out7;
  wire [23:0] undriven, undriven_2, undriven_3, undriven_4, undriven_5, undriven_6;

  Decoder #(.select(3), .tristate("false"), .disabled(0), .enable("true")) decoder_1 (
    .out0(decoder_1_out0), .out1(decoder_1_out1), .out2(decoder_1_out2), .out3(decoder_1_out3),
    .out4(decoder_1_out4), .out5(decoder_1_out5), .out6(decoder_1_out6), .out7(decoder_1_out7),
    .sel(Address_Bus[4:2]), .en(CS));
  Decoder #(.select(3), .tristate("false"), .disabled(0), .enable("true")) decoder_2 (
    .out0(decoder_2_out0), .out1(decoder_2_out1), .out2(decoder_2_out2), .out3(decoder_2_out3),
    .out4(decoder_2_out4), .out5(decoder_2_out5), .out6(decoder_2_out6), .out7(decoder_2_out7),
    .sel(Address_Bus[7:5]), .en(CS));
  and and_1 (and_1_out, decoder_2_out0, decoder_1_out0);
  and and_2 (and_2_out, decoder_2_out0, decoder_1_out1);
  and and_3 (and_3_out, decoder_2_out0, decoder_1_out2);
  and and_4 (and_4_out, decoder_2_out0, decoder_1_out3);
  and and_5 (and_5_out, decoder_2_out0, decoder_1_out4);
  and and_6 (and_6_out, decoder_2_out0, decoder_1_out5);
  and and_7 (and_7_out, decoder_2_out0, decoder_1_out6);
  and and_8 (and_8_out, decoder_2_out0, decoder_1_out7);
  RAM #(.addrWidth(24), .dataWidth(32), .bus("separate"), .Select("high")) ram_1 (
    .addr(Address_Bus[31:8]), .din(Data_Bus_In), .data(Data_Bus_Out), .str(Store), .sel(and_1_out),
    .clk(CLK), .ld(Load), .clr(Clear));
  RAM #(.addrWidth(24), .dataWidth(32), .bus("separate"), .Select("high")) ram_2 (
    .addr(Address_Bus[31:8]), .din(Data_Bus_In), .data(Data_Bus_Out), .str(Store), .sel(and_2_out),
    .clk(CLK), .ld(Load), .clr(Clear));
  RAM #(.addrWidth(24), .dataWidth(32), .bus("separate"), .Select("high")) ram_3 (
    .addr(Address_Bus[31:8]), .din(Data_Bus_In), .data(Data_Bus_Out), .str(Store), .sel(and_3_out),
    .clk(CLK), .ld(Load), .clr(Clear));
  RAM #(.addrWidth(24), .dataWidth(32), .bus("separate"), .Select("high")) ram_4 (
    .addr(Address_Bus[31:8]), .din(Data_Bus_In), .data(Data_Bus_Out), .str(Store), .sel(and_4_out),
    .clk(CLK), .ld(Load), .clr(Clear));
  RAM #(.addrWidth(24), .dataWidth(32), .bus("separate"), .Select("high")) ram_5 (
    .addr(Address_Bus[31:8]), .din(Data_Bus_In), .data(Data_Bus_Out), .str(Store), .sel(and_5_out),
    .clk(CLK), .ld(Load), .clr(Clear));
  RAM #(.addrWidth(24), .dataWidth(32), .bus("separate"), .Select("high")) ram_6 (
    .addr(Address_Bus[31:8]), .din(Data_Bus_In), .data(Data_Bus_Out), .str(Store), .sel(and_6_out),
    .clk(CLK), .ld(Load), .clr(Clear));
  RAM #(.addrWidth(24), .dataWidth(32), .bus("separate"), .Select("high")) ram_7 (
    .addr(Address_Bus[31:8]), .din(Data_Bus_In), .data(Data_Bus_Out), .str(Store), .sel(and_7_out),
    .clk(CLK), .ld(Load), .clr(Clear));
  RAM #(.addrWidth(24), .dataWidth(32), .bus("separate"), .Select("high")) ram_8 (
    .addr(Address_Bus[31:8]), .din(Data_Bus_In), .data(Data_Bus_Out), .str(Store), .sel(and_8_out),
    .clk(CLK), .ld(Load), .clr(Clear));
  and and_9 (and_9_out, decoder_2_out1, decoder_1_out0);
  and and_10 (and_10_out, decoder_2_out1, decoder_1_out1);
  and and_11 (and_11_out, decoder_2_out1, decoder_1_out2);
  and and_12 (and_12_out, decoder_2_out1, decoder_1_out3);
  and and_13 (and_13_out, decoder_2_out1, decoder_1_out4);
  and and_14 (and_14_out, decoder_2_out1, decoder_1_out5);
  and and_15 (and_15_out, decoder_2_out1, decoder_1_out6);
  and and_16 (and_16_out, decoder_2_out1, decoder_1_out7);
  RAM #(.addrWidth(24), .dataWidth(32), .bus("separate"), .Select("high")) ram_9 (
    .addr(Address_Bus[31:8]), .din(Data_Bus_In), .data(Data_Bus_Out), .str(Store), .sel(and_9_out),
    .clk(CLK), .ld(Load), .clr(Clear));
  RAM #(.addrWidth(24), .dataWidth(32), .bus("separate"), .Select("high")) ram_10 (
    .addr(Address_Bus[31:8]), .din(Data_Bus_In), .data(Data_Bus_Out), .str(Store), .sel(and_10_out),
    .clk(CLK), .ld(Load), .clr(Clear));
  RAM #(.addrWidth(24), .dataWidth(32), .bus("separate"), .Select("high")) ram_11 (
    .addr(Address_Bus[31:8]), .din(Data_Bus_In), .data(Data_Bus_Out), .str(Store), .sel(and_11_out),
    .clk(CLK), .ld(Load), .clr(Clear));
  RAM #(.addrWidth(24), .dataWidth(32), .bus("separate"), .Select("high")) ram_12 (
    .addr(Address_Bus[31:8]), .din(Data_Bus_In), .data(Data_Bus_Out), .str(Store), .sel(and_12_out),
    .clk(CLK), .ld(Load), .clr(Clear));
  RAM #(.addrWidth(24), .dataWidth(32), .bus("separate"), .Select("high")) ram_13 (
    .addr(Address_Bus[31:8]), .din(Data_Bus_In), .data(Data_Bus_Out), .str(Store), .sel(and_13_out),
    .clk(CLK), .ld(Load), .clr(Clear));
  RAM #(.addrWidth(24), .dataWidth(32), .bus("separate"), .Select("high")) ram_14 (
    .addr(Address_Bus[31:8]), .din(Data_Bus_In), .data(Data_Bus_Out), .str(Store), .sel(and_14_out),
    .clk(CLK), .ld(Load), .clr(Clear));
  RAM #(.addrWidth(24), .dataWidth(32), .bus("separate"), .Select("high")) ram_15 (
    .addr(Address_Bus[31:8]), .din(Data_Bus_In), .data(Data_Bus_Out), .str(Store), .sel(and_15_out),
    .clk(CLK), .ld(Load), .clr(Clear));
  RAM #(.addrWidth(24), .dataWidth(32), .bus("separate"), .Select("high")) ram_16 (
    .addr(Address_Bus[31:8]), .din(Data_Bus_In), .data(Data_Bus_Out), .str(Store), .sel(and_16_out),
    .clk(CLK), .ld(Load), .clr(Clear));
  and and_17 (and_17_out, decoder_2_out2, decoder_1_out0);
  and and_18 (and_18_out, decoder_2_out2, decoder_1_out1);
  and and_19 (and_19_out, decoder_2_out2, decoder_1_out2);
  and and_20 (and_20_out, decoder_2_out2, decoder_1_out3);
  and and_21 (and_21_out, decoder_2_out2, decoder_1_out4);
  and and_22 (and_22_out, decoder_2_out2, decoder_1_out5);
  and and_23 (and_23_out, decoder_2_out2, decoder_1_out6);
  and and_24 (and_24_out, decoder_2_out2, decoder_1_out7);
  RAM #(.addrWidth(24), .dataWidth(32), .bus("separate"), .Select("high")) ram_17 (
    .addr(Address_Bus[31:8]), .din(Data_Bus_In), .data(Data_Bus_Out), .str(Store), .sel(and_17_out),
    .clk(CLK), .ld(Load), .clr(Clear));
  RAM #(.addrWidth(24), .dataWidth(32), .bus("separate"), .Select("high")) ram_18 (
    .addr(Address_Bus[31:8]), .din(Data_Bus_In), .data(Data_Bus_Out), .str(Store), .sel(and_18_out),
    .clk(CLK), .ld(Load), .clr(Clear));
  RAM #(.addrWidth(24), .dataWidth(32), .bus("separate"), .Select("high")) ram_19 (
    .addr(Address_Bus[31:8]), .din(Data_Bus_In), .data(Data_Bus_Out), .str(Store), .sel(and_19_out),
    .clk(CLK), .ld(Load), .clr(Clear));
  RAM #(.addrWidth(24), .dataWidth(32), .bus("separate"), .Select("high")) ram_20 (
    .addr(Address_Bus[31:8]), .din(Data_Bus_In), .data(Data_Bus_Out), .str(Store), .sel(and_20_out),
    .clk(CLK), .ld(Load), .clr(Clear));
  RAM #(.addrWidth(24), .dataWidth(32), .bus("separate"), .Select("high")) ram_21 (
    .addr(Address_Bus[31:8]), .din(Data_Bus_In), .data(Data_Bus_Out), .str(Store), .sel(and_21_out),
    .clk(CLK), .ld(Load), .clr(Clear));
  RAM #(.addrWidth(24), .dataWidth(32), .bus("separate"), .Select("high")) ram_22 (
    .addr(Address_Bus[31:8]), .din(Data_Bus_In), .data(Data_Bus_Out), .str(Store), .sel(and_22_out),
    .clk(CLK), .ld(Load), .clr(Clear));
  RAM #(.addrWidth(24), .dataWidth(32), .bus("separate"), .Select("high")) ram_23 (
    .addr(Address_Bus[31:8]), .din(Data_Bus_In), .data(Data_Bus_Out), .str(Store), .sel(and_23_out),
    .clk(CLK), .ld(Load), .clr(Clear));
  RAM #(.addrWidth(24), .dataWidth(32), .bus("separate"), .Select("high")) ram_24 (
    .addr(Address_Bus[31:8]), .din(Data_Bus_In), .data(Data_Bus_Out), .str(Store), .sel(and_24_out),
    .clk(CLK), .ld(Load), .clr(Clear));
  and and_25 (and_25_out, decoder_2_out3, decoder_1_out0);
  and and_26 (and_26_out, decoder_2_out3, decoder_1_out1);
  and and_27 (and_27_out, decoder_2_out3, decoder_1_out2);
  and and_28 (and_28_out, decoder_2_out3, decoder_1_out3);
  and and_29 (and_29_out, decoder_2_out3, decoder_1_out4);
  and and_30 (and_30_out, decoder_2_out3, decoder_1_out5);
  and and_31 (and_31_out, decoder_2_out3, decoder_1_out6);
  and and_32 (and_32_out, decoder_2_out3, decoder_1_out7);
  RAM #(.addrWidth(24), .dataWidth(32), .bus("separate"), .Select("high")) ram_25 (
    .addr(Address_Bus[31:8]), .din(Data_Bus_In), .data(Data_Bus_Out), .str(Store), .sel(and_25_out),
    .clk(CLK), .ld(Load), .clr(Clear));
  RAM #(.addrWidth(24), .dataWidth(32), .bus("separate"), .Select("high")) ram_26 (
    .addr(Address_Bus[31:8]), .din(Data_Bus_In), .data(Data_Bus_Out), .str(Store), .sel(and_26_out),
    .clk(CLK), .ld(Load), .clr(Clear));
  RAM #(.addrWidth(24), .dataWidth(32), .bus("separate"), .Select("high")) ram_27 (
    .addr(Address_Bus[31:8]), .din(Data_Bus_In), .data(Data_Bus_Out), .str(Store), .sel(and_27_out),
    .clk(CLK), .ld(Load), .clr(Clear));
  RAM #(.addrWidth(24), .dataWidth(32), .bus("separate"), .Select("high")) ram_28 (
    .addr(Address_Bus[31:8]), .din(Data_Bus_In), .data(Data_Bus_Out), .str(Store), .sel(and_28_out),
    .clk(CLK), .ld(Load), .clr(Clear));
  RAM #(.addrWidth(24), .dataWidth(32), .bus("separate"), .Select("high")) ram_29 (
    .addr(Address_Bus[31:8]), .din(Data_Bus_In), .data(Data_Bus_Out), .str(Store), .sel(and_29_out),
    .clk(CLK), .ld(Load), .clr(Clear));
  RAM #(.addrWidth(24), .dataWidth(32), .bus("separate"), .Select("high")) ram_30 (
    .addr(Address_Bus[31:8]), .din(Data_Bus_In), .data(Data_Bus_Out), .str(Store), .sel(and_30_out),
    .clk(CLK), .ld(Load), .clr(Clear));
  RAM #(.addrWidth(24), .dataWidth(32), .bus("separate"), .Select("high")) ram_31 (
    .addr(Address_Bus[31:8]), .din(Data_Bus_In), .data(Data_Bus_Out), .str(Store), .sel(and_31_out),
    .clk(CLK), .ld(Load), .clr(Clear));
  RAM #(.addrWidth(24), .dataWidth(32), .bus("separate"), .Select("high")) ram_32 (
    .addr(Address_Bus[31:8]), .din(Data_Bus_In), .data(Data_Bus_Out), .str(Store), .sel(and_32_out),
    .clk(CLK), .ld(Load), .clr(Clear));
  and and_33 (and_33_out, decoder_2_out4, decoder_1_out0);
  and and_34 (and_34_out, decoder_2_out4, decoder_1_out1);
  and and_35 (and_35_out, decoder_2_out4, decoder_1_out2);
  and and_36 (and_36_out, decoder_2_out4, decoder_1_out3);
  and and_37 (and_37_out, decoder_2_out4, decoder_1_out4);
  and and_38 (and_38_out, decoder_2_out4, decoder_1_out5);
  and and_39 (and_39_out, decoder_2_out4, decoder_1_out6);
  and and_40 (and_40_out, decoder_2_out4, decoder_1_out7);
  RAM #(.addrWidth(24), .dataWidth(32), .bus("separate"), .Select("high")) ram_33 (
    .addr(Address_Bus[31:8]), .din(Data_Bus_In), .data(Data_Bus_Out), .str(Store), .sel(and_33_out),
    .clk(CLK), .ld(Load), .clr(Clear));
  RAM #(.addrWidth(24), .dataWidth(32), .bus("separate"), .Select("high")) ram_34 (
    .addr(Address_Bus[31:8]), .din(Data_Bus_In), .data(Data_Bus_Out), .str(Store), .sel(and_34_out),
    .clk(CLK), .ld(Load), .clr(Clear));
  RAM #(.addrWidth(24), .dataWidth(32), .bus("separate"), .Select("high")) ram_35 (
    .addr(Address_Bus[31:8]), .din(Data_Bus_In), .data(Data_Bus_Out), .str(Store), .sel(and_35_out),
    .clk(CLK), .ld(Load), .clr(Clear));
  RAM #(.addrWidth(24), .dataWidth(32), .bus("separate"), .Select("high")) ram_36 (
    .addr(Address_Bus[31:8]), .din(Data_Bus_In), .data(Data_Bus_Out), .str(Store), .sel(and_36_out),
    .clk(CLK), .ld(Load), .clr(Clear));
  RAM #(.addrWidth(24), .dataWidth(32), .bus("separate"), .Select("high")) ram_37 (
    .addr(Address_Bus[31:8]), .din(Data_Bus_In), .data(Data_Bus_Out), .str(Store), .sel(and_37_out),
    .clk(CLK), .ld(Load), .clr(Clear));
  RAM #(.addrWidth(24), .dataWidth(32), .bus("separate"), .Select("high")) ram_38 (
    .addr(Address_Bus[31:8]), .din(Data_Bus_In), .data(Data_Bus_Out), .str(Store), .sel(and_38_out),
    .clk(CLK), .ld(Load), .clr(Clear));
  RAM #(.addrWidth(24), .dataWidth(32), .bus("separate"), .Select("high")) ram_39 (
    .addr(Address_Bus[31:8]), .din(Data_Bus_In), .data(Data_Bus_Out), .str(Store), .sel(and_39_out),
    .clk(CLK), .ld(Load), .clr(Clear));
  RAM #(.addrWidth(24), .dataWidth(32), .bus("separate"), .Select("high")) ram_40 (
    .addr(Address_Bus[31:8]), .din(Data_Bus_In), .data(Data_Bus_Out), .str(Store), .sel(and_40_out),
    .clk(CLK), .ld(Load), .clr(Clear));
  and and_41 (and_41_out, decoder_2_out5, decoder_1_out0);
  and and_42 (and_42_out, decoder_2_out5, decoder_1_out1);
  and and_43 (and_43_out, decoder_2_out5, decoder_1_out2);
  and and_44 (and_44_out, decoder_2_out5, decoder_1_out3);
  and and_45 (and_45_out, decoder_2_out5, decoder_1_out4);
  and and_46 (and_46_out, decoder_2_out5, decoder_1_out5);
  and and_47 (and_47_out, decoder_2_out5, decoder_1_out6);
  and and_48 (and_48_out, decoder_2_out5, decoder_1_out7);
  RAM #(.addrWidth(24), .dataWidth(32), .bus("separate"), .Select("high")) ram_41 (
    .addr(undriven), .din(Data_Bus_In), .data(Data_Bus_Out), .str(Store), .sel(and_41_out), .clk(CLK),
    .ld(Load), .clr(Clear));
  RAM #(.addrWidth(24), .dataWidth(32), .bus("separate"), .Select("high")) ram_42 (
    .addr(undriven), .din(Data_Bus_In), .data(Data_Bus_Out), .str(Store), .sel(and_42_out), .clk(CLK),
    .ld(Load), .clr(Clear));
  RAM #(.addrWidth(24), .dataWidth(32), .bus("separate"), .Select("high")) ram_43 (
    .addr(undriven_2), .din(Data_Bus_In), .data(Data_Bus_Out), .str(Store), .sel(and_43_out), .clk(CLK),
    .ld(Load), .clr(Clear));
  RAM #(.addrWidth(24), .dataWidth(32), .bus("separate"), .Select("high")) ram_44 (
    .addr(undriven_3), .din(Data_Bus_In), .data(Data_Bus_Out), .str(Store), .sel(and_44_out), .clk(CLK),
    .ld(Load), .clr(Clear));
  RAM #(.addrWidth(24), .dataWidth(32), .bus("separate"), .Select("high")) ram_45 (
    .addr(undriven_4), .din(Data_Bus_In), .data(Data_Bus_Out), .str(Store), .sel(and_45_out), .clk(CLK),
    .ld(Load), .clr(Clear));
  RAM #(.addrWidth(24), .dataWidth(32), .bus("separate"), .Select("high")) ram_46 (
    .addr(undriven_5), .din(Data_Bus_In), .data(Data_Bus_Out), .str(Store), .sel(and_46_out), .clk(CLK),
    .ld(Load), .clr(Clear));
  RAM #(.addrWidth(24), .dataWidth(32), .bus("separate"), .Select("high")) ram_47 (
    .addr(undriven_6), .din(Data_Bus_In), .data(Data_Bus_Out), .str(Store), .sel(and_47_out), .clk(CLK),
    .ld(Load), .clr(Clear));
  RAM #(.addrWidth(24), .dataWidth(32), .bus("separate"), .Select("high")) ram_48 (
    .addr(Address_Bus[31:8]), .din(Data_Bus_In), .data(Data_Bus_Out), .str(Store), .sel(and_48_out),
    .clk(CLK), .ld(Load), .clr(Clear));
  and and_49 (and_49_out, decoder_2_out6, decoder_1_out0);
  and and_50 (and_50_out, decoder_2_out6, decoder_1_out1);
  and and_51 (and_51_out, decoder_2_out6, decoder_1_out2);
  and and_52 (and_52_out, decoder_2_out6, decoder_1_out3);
  and and_53 (and_53_out, decoder_2_out6, decoder_1_out4);
  and and_54 (and_54_out, decoder_2_out6, decoder_1_out5);
  and and_55 (and_55_out, decoder_2_out6, decoder_1_out6);
  and and_56 (and_56_out, decoder_2_out6, decoder_1_out7);
  RAM #(.addrWidth(24), .dataWidth(32), .bus("separate"), .Select("high")) ram_49 (
    .addr(Address_Bus[31:8]), .din(Data_Bus_In), .data(Data_Bus_Out), .str(Store), .sel(and_49_out),
    .clk(CLK), .ld(Load), .clr(Clear));
  RAM #(.addrWidth(24), .dataWidth(32), .bus("separate"), .Select("high")) ram_50 (
    .addr(Address_Bus[31:8]), .din(Data_Bus_In), .data(Data_Bus_Out), .str(Store), .sel(and_50_out),
    .clk(CLK), .ld(Load), .clr(Clear));
  RAM #(.addrWidth(24), .dataWidth(32), .bus("separate"), .Select("high")) ram_51 (
    .addr(Address_Bus[31:8]), .din(Data_Bus_In), .data(Data_Bus_Out), .str(Store), .sel(and_51_out),
    .clk(CLK), .ld(Load), .clr(Clear));
  RAM #(.addrWidth(24), .dataWidth(32), .bus("separate"), .Select("high")) ram_52 (
    .addr(Address_Bus[31:8]), .din(Data_Bus_In), .data(Data_Bus_Out), .str(Store), .sel(and_52_out),
    .clk(CLK), .ld(Load), .clr(Clear));
  RAM #(.addrWidth(24), .dataWidth(32), .bus("separate"), .Select("high")) ram_53 (
    .addr(Address_Bus[31:8]), .din(Data_Bus_In), .data(Data_Bus_Out), .str(Store), .sel(and_53_out),
    .clk(CLK), .ld(Load), .clr(Clear));
  RAM #(.addrWidth(24), .dataWidth(32), .bus("separate"), .Select("high")) ram_54 (
    .addr(Address_Bus[31:8]), .din(Data_Bus_In), .data(Data_Bus_Out), .str(Store), .sel(and_54_out),
    .clk(CLK), .ld(Load), .clr(Clear));
  RAM #(.addrWidth(24), .dataWidth(32), .bus("separate"), .Select("high")) ram_55 (
    .addr(Address_Bus[31:8]), .din(Data_Bus_In), .data(Data_Bus_Out), .str(Store), .sel(and_55_out),
    .clk(CLK), .ld(Load), .clr(Clear));
  RAM #(.addrWidth(24), .dataWidth(32), .bus("separate"), .Select("high")) ram_56 (
    .addr(Address_Bus[31:8]), .din(Data_Bus_In), .data(Data_Bus_Out), .str(Store), .sel(and_56_out),
    .clk(CLK), .ld(Load), .clr(Clear));
  and and_57 (and_57_out, decoder_2_out7, decoder_1_out0);
  and and_58 (and_58_out, decoder_2_out7, decoder_1_out1);
  and and_59 (and_59_out, decoder_2_out7, decoder_1_out2);
  and and_60 (and_60_out, decoder_2_out7, decoder_1_out3);
  and and_61 (and_61_out, decoder_2_out7, decoder_1_out4);
  and and_62 (and_62_out, decoder_2_out7, decoder_1_out5);
  and and_63 (and_63_out, decoder_2_out7, decoder_1_out6);
  and and_64 (and_64_out, decoder_2_out7, decoder_1_out7);
  RAM #(.addrWidth(24), .dataWidth(32), .bus("separate"), .Select("high")) ram_57 (
    .addr(Address_Bus[31:8]), .din(Data_Bus_In), .data(Data_Bus_Out), .str(Store), .sel(and_57_out),
    .clk(CLK), .ld(Load), .clr(Clear));
  RAM #(.addrWidth(24), .dataWidth(32), .bus("separate"), .Select("high")) ram_58 (
    .addr(Address_Bus[31:8]), .din(Data_Bus_In), .data(Data_Bus_Out), .str(Store), .sel(and_58_out),
    .clk(CLK), .ld(Load), .clr(Clear));
  RAM #(.addrWidth(24), .dataWidth(32), .bus("separate"), .Select("high")) ram_59 (
    .addr(Address_Bus[31:8]), .din(Data_Bus_In), .data(Data_Bus_Out), .str(Store), .sel(and_59_out),
    .clk(CLK), .ld(Load), .clr(Clear));
  RAM #(.addrWidth(24), .dataWidth(32), .bus("separate"), .Select("high")) ram_60 (
    .addr(Address_Bus[31:8]), .din(Data_Bus_In), .data(Data_Bus_Out), .str(Store), .sel(and_60_out),
    .clk(CLK), .ld(Load), .clr(Clear));
  RAM #(.addrWidth(24), .dataWidth(32), .bus("separate"), .Select("high")) ram_61 (
    .addr(Address_Bus[31:8]), .din(Data_Bus_In), .data(Data_Bus_Out), .str(Store), .sel(and_61_out),
    .clk(CLK), .ld(Load), .clr(Clear));
  RAM #(.addrWidth(24), .dataWidth(32), .bus("separate"), .Select("high")) ram_62 (
    .addr(Address_Bus[31:8]), .din(Data_Bus_In), .data(Data_Bus_Out), .str(Store), .sel(and_62_out),
    .clk(CLK), .ld(Load), .clr(Clear));
  RAM #(.addrWidth(24), .dataWidth(32), .bus("separate"), .Select("high")) ram_63 (
    .addr(Address_Bus[31:8]), .din(Data_Bus_In), .data(Data_Bus_Out), .str(Store), .sel(and_63_out),
    .clk(CLK), .ld(Load), .clr(Clear));
  RAM #(.addrWidth(24), .dataWidth(32), .bus("separate"), .Select("high")) ram_64 (
    .addr(Address_Bus[31:8]), .din(Data_Bus_In), .data(Data_Bus_Out), .str(Store), .sel(and_64_out),
    .clk(CLK), .ld(Load), .clr(Clear));

  // Other names for the same wires on the sheet: Ad_TP[31:0] = Address_Bus; _24位[23:0] = Address_Bus[31:8];
  //   Data_Bus_In_TP[31:0] = Data_Bus_In; DataOut[31:0] = Data_Bus_Out

  // Notes on the sheet:
  //   外部各接口定义与原RAM相同
  //   按照字节编址，但按照字对齐访问
endmodule

module \_32位地址总线32位数据总线ROM存储器  (
  input  CS,
  input  [31:0] Address_Bus,
  output [31:0] Data_Bus_Out
);

  wire and_1_out, and_2_out, and_3_out, and_4_out, and_5_out, and_6_out, and_7_out, and_8_out, and_9_out,
       and_10_out, and_11_out, and_12_out, and_13_out, and_14_out, and_15_out, and_16_out, and_17_out,
       and_18_out, and_19_out, and_20_out, and_21_out, and_22_out, and_23_out, and_24_out, and_25_out,
       and_26_out, and_27_out, and_28_out, and_29_out, and_30_out, and_31_out, and_32_out, and_33_out,
       and_34_out, and_35_out, and_36_out, and_37_out, and_38_out, and_39_out, and_40_out, and_41_out,
       and_42_out, and_43_out, and_44_out, and_45_out, and_46_out, and_47_out, and_48_out, and_49_out,
       and_50_out, and_51_out, and_52_out, and_53_out, and_54_out, and_55_out, and_56_out, and_57_out,
       and_58_out, and_59_out, and_60_out, and_61_out, and_62_out, and_63_out, and_64_out, decoder_1_out0,
       decoder_1_out1, decoder_1_out2, decoder_1_out3, decoder_1_out4, decoder_1_out5, decoder_1_out6,
       decoder_1_out7, decoder_2_out0, decoder_2_out1, decoder_2_out2, decoder_2_out3, decoder_2_out4,
       decoder_2_out5, decoder_2_out6, decoder_2_out7;

  Decoder #(.select(3), .tristate("false"), .disabled(0), .enable("true")) decoder_1 (
    .out0(decoder_1_out0), .out1(decoder_1_out1), .out2(decoder_1_out2), .out3(decoder_1_out3),
    .out4(decoder_1_out4), .out5(decoder_1_out5), .out6(decoder_1_out6), .out7(decoder_1_out7),
    .sel(Address_Bus[28:26]), .en(CS));
  Decoder #(.select(3), .tristate("false"), .disabled(0), .enable("true")) decoder_2 (
    .out0(decoder_2_out0), .out1(decoder_2_out1), .out2(decoder_2_out2), .out3(decoder_2_out3),
    .out4(decoder_2_out4), .out5(decoder_2_out5), .out6(decoder_2_out6), .out7(decoder_2_out7),
    .sel(Address_Bus[31:29]), .en(CS));
  and and_1 (and_1_out, decoder_2_out0, decoder_1_out0);
  and and_2 (and_2_out, decoder_2_out0, decoder_1_out1);
  and and_3 (and_3_out, decoder_2_out0, decoder_1_out2);
  and and_4 (and_4_out, decoder_2_out0, decoder_1_out3);
  and and_5 (and_5_out, decoder_2_out0, decoder_1_out4);
  and and_6 (and_6_out, decoder_2_out0, decoder_1_out5);
  and and_7 (and_7_out, decoder_2_out0, decoder_1_out6);
  and and_8 (and_8_out, decoder_2_out0, decoder_1_out7);
  ROM #(.addrWidth(24), .dataWidth(32), .Select("high")) rom_1 (
    .addr(Address_Bus[25:2]), .data(Data_Bus_Out), .sel(and_1_out));
  ROM #(.addrWidth(24), .dataWidth(32), .Select("high")) rom_2 (
    .addr(Address_Bus[25:2]), .data(Data_Bus_Out), .sel(and_2_out));
  ROM #(.addrWidth(24), .dataWidth(32), .Select("high")) rom_3 (
    .addr(Address_Bus[25:2]), .data(Data_Bus_Out), .sel(and_3_out));
  ROM #(.addrWidth(24), .dataWidth(32), .Select("high")) rom_4 (
    .addr(Address_Bus[25:2]), .data(Data_Bus_Out), .sel(and_4_out));
  ROM #(.addrWidth(24), .dataWidth(32), .Select("high")) rom_5 (
    .addr(Address_Bus[25:2]), .data(Data_Bus_Out), .sel(and_5_out));
  ROM #(.addrWidth(24), .dataWidth(32), .Select("high")) rom_6 (
    .addr(Address_Bus[25:2]), .data(Data_Bus_Out), .sel(and_6_out));
  ROM #(.addrWidth(24), .dataWidth(32), .Select("high")) rom_7 (
    .addr(Address_Bus[25:2]), .data(Data_Bus_Out), .sel(and_7_out));
  ROM #(.addrWidth(24), .dataWidth(32), .Select("high")) rom_8 (
    .addr(Address_Bus[25:2]), .data(Data_Bus_Out), .sel(and_8_out));
  and and_9 (and_9_out, decoder_2_out1, decoder_1_out0);
  and and_10 (and_10_out, decoder_2_out1, decoder_1_out1);
  and and_11 (and_11_out, decoder_2_out1, decoder_1_out2);
  and and_12 (and_12_out, decoder_2_out1, decoder_1_out3);
  and and_13 (and_13_out, decoder_2_out1, decoder_1_out4);
  and and_14 (and_14_out, decoder_2_out1, decoder_1_out5);
  and and_15 (and_15_out, decoder_2_out1, decoder_1_out6);
  and and_16 (and_16_out, decoder_2_out1, decoder_1_out7);
  ROM #(.addrWidth(24), .dataWidth(32), .Select("high")) rom_9 (
    .addr(Address_Bus[25:2]), .data(Data_Bus_Out), .sel(and_9_out));
  ROM #(.addrWidth(24), .dataWidth(32), .Select("high")) rom_10 (
    .addr(Address_Bus[25:2]), .data(Data_Bus_Out), .sel(and_10_out));
  ROM #(.addrWidth(24), .dataWidth(32), .Select("high")) rom_11 (
    .addr(Address_Bus[25:2]), .data(Data_Bus_Out), .sel(and_11_out));
  ROM #(.addrWidth(24), .dataWidth(32), .Select("high")) rom_12 (
    .addr(Address_Bus[25:2]), .data(Data_Bus_Out), .sel(and_12_out));
  ROM #(.addrWidth(24), .dataWidth(32), .Select("high")) rom_13 (
    .addr(Address_Bus[25:2]), .data(Data_Bus_Out), .sel(and_13_out));
  ROM #(.addrWidth(24), .dataWidth(32), .Select("high")) rom_14 (
    .addr(Address_Bus[25:2]), .data(Data_Bus_Out), .sel(and_14_out));
  ROM #(.addrWidth(24), .dataWidth(32), .Select("high")) rom_15 (
    .addr(Address_Bus[25:2]), .data(Data_Bus_Out), .sel(and_15_out));
  ROM #(.addrWidth(24), .dataWidth(32), .Select("high")) rom_16 (
    .addr(Address_Bus[25:2]), .data(Data_Bus_Out), .sel(and_16_out));
  and and_17 (and_17_out, decoder_2_out2, decoder_1_out0);
  and and_18 (and_18_out, decoder_2_out2, decoder_1_out1);
  and and_19 (and_19_out, decoder_2_out2, decoder_1_out2);
  and and_20 (and_20_out, decoder_2_out2, decoder_1_out3);
  and and_21 (and_21_out, decoder_2_out2, decoder_1_out4);
  and and_22 (and_22_out, decoder_2_out2, decoder_1_out5);
  and and_23 (and_23_out, decoder_2_out2, decoder_1_out6);
  and and_24 (and_24_out, decoder_2_out2, decoder_1_out7);
  ROM #(.addrWidth(24), .dataWidth(32), .Select("high")) rom_17 (
    .addr(Address_Bus[25:2]), .data(Data_Bus_Out), .sel(and_17_out));
  ROM #(.addrWidth(24), .dataWidth(32), .Select("high")) rom_18 (
    .addr(Address_Bus[25:2]), .data(Data_Bus_Out), .sel(and_18_out));
  ROM #(.addrWidth(24), .dataWidth(32), .Select("high")) rom_19 (
    .addr(Address_Bus[25:2]), .data(Data_Bus_Out), .sel(and_19_out));
  ROM #(.addrWidth(24), .dataWidth(32), .Select("high")) rom_20 (
    .addr(Address_Bus[25:2]), .data(Data_Bus_Out), .sel(and_20_out));
  ROM #(.addrWidth(24), .dataWidth(32), .Select("high")) rom_21 (
    .addr(Address_Bus[25:2]), .data(Data_Bus_Out), .sel(and_21_out));
  ROM #(.addrWidth(24), .dataWidth(32), .Select("high")) rom_22 (
    .addr(Address_Bus[25:2]), .data(Data_Bus_Out), .sel(and_22_out));
  ROM #(.addrWidth(24), .dataWidth(32), .Select("high")) rom_23 (
    .addr(Address_Bus[25:2]), .data(Data_Bus_Out), .sel(and_23_out));
  ROM #(.addrWidth(24), .dataWidth(32), .Select("high")) rom_24 (
    .addr(Address_Bus[25:2]), .data(Data_Bus_Out), .sel(and_24_out));
  and and_25 (and_25_out, decoder_2_out3, decoder_1_out0);
  and and_26 (and_26_out, decoder_2_out3, decoder_1_out1);
  and and_27 (and_27_out, decoder_2_out3, decoder_1_out2);
  and and_28 (and_28_out, decoder_2_out3, decoder_1_out3);
  and and_29 (and_29_out, decoder_2_out3, decoder_1_out4);
  and and_30 (and_30_out, decoder_2_out3, decoder_1_out5);
  and and_31 (and_31_out, decoder_2_out3, decoder_1_out6);
  and and_32 (and_32_out, decoder_2_out3, decoder_1_out7);
  ROM #(.addrWidth(24), .dataWidth(32), .Select("high")) rom_25 (
    .addr(Address_Bus[25:2]), .data(Data_Bus_Out), .sel(and_25_out));
  ROM #(.addrWidth(24), .dataWidth(32), .Select("high")) rom_26 (
    .addr(Address_Bus[25:2]), .data(Data_Bus_Out), .sel(and_26_out));
  ROM #(.addrWidth(24), .dataWidth(32), .Select("high")) rom_27 (
    .addr(Address_Bus[25:2]), .data(Data_Bus_Out), .sel(and_27_out));
  ROM #(.addrWidth(24), .dataWidth(32), .Select("high")) rom_28 (
    .addr(Address_Bus[25:2]), .data(Data_Bus_Out), .sel(and_28_out));
  ROM #(.addrWidth(24), .dataWidth(32), .Select("high")) rom_29 (
    .addr(Address_Bus[25:2]), .data(Data_Bus_Out), .sel(and_29_out));
  ROM #(.addrWidth(24), .dataWidth(32), .Select("high")) rom_30 (
    .addr(Address_Bus[25:2]), .data(Data_Bus_Out), .sel(and_30_out));
  ROM #(.addrWidth(24), .dataWidth(32), .Select("high")) rom_31 (
    .addr(Address_Bus[25:2]), .data(Data_Bus_Out), .sel(and_31_out));
  ROM #(.addrWidth(24), .dataWidth(32), .Select("high")) rom_32 (
    .addr(Address_Bus[25:2]), .data(Data_Bus_Out), .sel(and_32_out));
  and and_33 (and_33_out, decoder_2_out4, decoder_1_out0);
  and and_34 (and_34_out, decoder_2_out4, decoder_1_out1);
  and and_35 (and_35_out, decoder_2_out4, decoder_1_out2);
  and and_36 (and_36_out, decoder_2_out4, decoder_1_out3);
  and and_37 (and_37_out, decoder_2_out4, decoder_1_out4);
  and and_38 (and_38_out, decoder_2_out4, decoder_1_out5);
  and and_39 (and_39_out, decoder_2_out4, decoder_1_out6);
  and and_40 (and_40_out, decoder_2_out4, decoder_1_out7);
  ROM #(.addrWidth(24), .dataWidth(32), .Select("high")) rom_33 (
    .addr(Address_Bus[25:2]), .data(Data_Bus_Out), .sel(and_33_out));
  ROM #(.addrWidth(24), .dataWidth(32), .Select("high")) rom_34 (
    .addr(Address_Bus[25:2]), .data(Data_Bus_Out), .sel(and_34_out));
  ROM #(.addrWidth(24), .dataWidth(32), .Select("high")) rom_35 (
    .addr(Address_Bus[25:2]), .data(Data_Bus_Out), .sel(and_35_out));
  ROM #(.addrWidth(24), .dataWidth(32), .Select("high")) rom_36 (
    .addr(Address_Bus[25:2]), .data(Data_Bus_Out), .sel(and_36_out));
  ROM #(.addrWidth(24), .dataWidth(32), .Select("high")) rom_37 (
    .addr(Address_Bus[25:2]), .data(Data_Bus_Out), .sel(and_37_out));
  ROM #(.addrWidth(24), .dataWidth(32), .Select("high")) rom_38 (
    .addr(Address_Bus[25:2]), .data(Data_Bus_Out), .sel(and_38_out));
  ROM #(.addrWidth(24), .dataWidth(32), .Select("high")) rom_39 (
    .addr(Address_Bus[25:2]), .data(Data_Bus_Out), .sel(and_39_out));
  ROM #(.addrWidth(24), .dataWidth(32), .Select("high")) rom_40 (
    .addr(Address_Bus[25:2]), .data(Data_Bus_Out), .sel(and_40_out));
  and and_41 (and_41_out, decoder_2_out5, decoder_1_out0);
  and and_42 (and_42_out, decoder_2_out5, decoder_1_out1);
  and and_43 (and_43_out, decoder_2_out5, decoder_1_out2);
  and and_44 (and_44_out, decoder_2_out5, decoder_1_out3);
  and and_45 (and_45_out, decoder_2_out5, decoder_1_out4);
  and and_46 (and_46_out, decoder_2_out5, decoder_1_out5);
  and and_47 (and_47_out, decoder_2_out5, decoder_1_out6);
  and and_48 (and_48_out, decoder_2_out5, decoder_1_out7);
  ROM #(.addrWidth(24), .dataWidth(32), .Select("high")) rom_41 (
    .addr(Address_Bus[25:2]), .data(Data_Bus_Out), .sel(and_41_out));
  ROM #(.addrWidth(24), .dataWidth(32), .Select("high")) rom_42 (
    .addr(Address_Bus[25:2]), .data(Data_Bus_Out), .sel(and_42_out));
  ROM #(.addrWidth(24), .dataWidth(32), .Select("high")) rom_43 (
    .addr(Address_Bus[25:2]), .data(Data_Bus_Out), .sel(and_43_out));
  ROM #(.addrWidth(24), .dataWidth(32), .Select("high")) rom_44 (
    .addr(Address_Bus[25:2]), .data(Data_Bus_Out), .sel(and_44_out));
  ROM #(.addrWidth(24), .dataWidth(32), .Select("high")) rom_45 (
    .addr(Address_Bus[25:2]), .data(Data_Bus_Out), .sel(and_45_out));
  ROM #(.addrWidth(24), .dataWidth(32), .Select("high")) rom_46 (
    .addr(Address_Bus[25:2]), .data(Data_Bus_Out), .sel(and_46_out));
  ROM #(.addrWidth(24), .dataWidth(32), .Select("high")) rom_47 (
    .addr(Address_Bus[25:2]), .data(Data_Bus_Out), .sel(and_47_out));
  ROM #(.addrWidth(24), .dataWidth(32), .Select("high")) rom_48 (
    .addr(Address_Bus[25:2]), .data(Data_Bus_Out), .sel(and_48_out));
  and and_49 (and_49_out, decoder_2_out6, decoder_1_out0);
  and and_50 (and_50_out, decoder_2_out6, decoder_1_out1);
  and and_51 (and_51_out, decoder_2_out6, decoder_1_out2);
  and and_52 (and_52_out, decoder_2_out6, decoder_1_out3);
  and and_53 (and_53_out, decoder_2_out6, decoder_1_out4);
  and and_54 (and_54_out, decoder_2_out6, decoder_1_out5);
  and and_55 (and_55_out, decoder_2_out6, decoder_1_out6);
  and and_56 (and_56_out, decoder_2_out6, decoder_1_out7);
  ROM #(.addrWidth(24), .dataWidth(32), .Select("high")) rom_49 (
    .addr(Address_Bus[25:2]), .data(Data_Bus_Out), .sel(and_49_out));
  ROM #(.addrWidth(24), .dataWidth(32), .Select("high")) rom_50 (
    .addr(Address_Bus[25:2]), .data(Data_Bus_Out), .sel(and_50_out));
  ROM #(.addrWidth(24), .dataWidth(32), .Select("high")) rom_51 (
    .addr(Address_Bus[25:2]), .data(Data_Bus_Out), .sel(and_51_out));
  ROM #(.addrWidth(24), .dataWidth(32), .Select("high")) rom_52 (
    .addr(Address_Bus[25:2]), .data(Data_Bus_Out), .sel(and_52_out));
  ROM #(.addrWidth(24), .dataWidth(32), .Select("high")) rom_53 (
    .addr(Address_Bus[25:2]), .data(Data_Bus_Out), .sel(and_53_out));
  ROM #(.addrWidth(24), .dataWidth(32), .Select("high")) rom_54 (
    .addr(Address_Bus[25:2]), .data(Data_Bus_Out), .sel(and_54_out));
  ROM #(.addrWidth(24), .dataWidth(32), .Select("high")) rom_55 (
    .addr(Address_Bus[25:2]), .data(Data_Bus_Out), .sel(and_55_out));
  ROM #(.addrWidth(24), .dataWidth(32), .Select("high")) rom_56 (
    .addr(Address_Bus[25:2]), .data(Data_Bus_Out), .sel(and_56_out));
  and and_57 (and_57_out, decoder_2_out7, decoder_1_out0);
  and and_58 (and_58_out, decoder_2_out7, decoder_1_out1);
  and and_59 (and_59_out, decoder_2_out7, decoder_1_out2);
  and and_60 (and_60_out, decoder_2_out7, decoder_1_out3);
  and and_61 (and_61_out, decoder_2_out7, decoder_1_out4);
  and and_62 (and_62_out, decoder_2_out7, decoder_1_out5);
  and and_63 (and_63_out, decoder_2_out7, decoder_1_out6);
  and and_64 (and_64_out, decoder_2_out7, decoder_1_out7);
  ROM #(.addrWidth(24), .dataWidth(32), .Select("high")) rom_57 (
    .addr(Address_Bus[25:2]), .data(Data_Bus_Out), .sel(and_57_out));
  ROM #(.addrWidth(24), .dataWidth(32), .Select("high")) rom_58 (
    .addr(Address_Bus[25:2]), .data(Data_Bus_Out), .sel(and_58_out));
  ROM #(.addrWidth(24), .dataWidth(32), .Select("high")) rom_59 (
    .addr(Address_Bus[25:2]), .data(Data_Bus_Out), .sel(and_59_out));
  ROM #(.addrWidth(24), .dataWidth(32), .Select("high")) rom_60 (
    .addr(Address_Bus[25:2]), .data(Data_Bus_Out), .sel(and_60_out));
  ROM #(.addrWidth(24), .dataWidth(32), .Select("high")) rom_61 (
    .addr(Address_Bus[25:2]), .data(Data_Bus_Out), .sel(and_61_out));
  ROM #(.addrWidth(24), .dataWidth(32), .Select("high")) rom_62 (
    .addr(Address_Bus[25:2]), .data(Data_Bus_Out), .sel(and_62_out));
  ROM #(.addrWidth(24), .dataWidth(32), .Select("high")) rom_63 (
    .addr(Address_Bus[25:2]), .data(Data_Bus_Out), .sel(and_63_out));
  ROM #(.addrWidth(24), .dataWidth(32), .Select("high")) rom_64 (
    .addr(Address_Bus[25:2]), .data(Data_Bus_Out), .sel(and_64_out));

  // Other names for the same wires on the sheet: Ad_TP[31:0] = Address_Bus; _24位[23:0] = Address_Bus[25:2];
  //   DataOut[31:0] = Data_Bus_Out

  // Notes on the sheet:
  //   contents of rom_1 (hex, n*v repeats v):
  //   20100001 20110000 ae300000 22100001 22310004 ae300000 22100001 22310004 ae300000 22100001 22310004
  //   ae300000 22100001 22310004 ae300000 22100001 22310004 ae300000 22100001 22310004 ae300000 22100001
  //   22310004 ae300000 8020 2011001c 8e130000 8e340000 274402a 11000002 ae330000 ae140000 2231fffc
  //   1611fff8 22100004 2011001c 1611fff5 c
  //   外部各接口定义与原ROM相同
  //   按照字节编址，但按照字对齐访问
endmodule

module \MIPS寄存器文件  (
  input  [4:0] A1_address,
  input  [31:0] W_data,
  input  [4:0] A2_address,
  input  [4:0] W_address,
  input  W_Enable,
  input  CLK,
  output [31:0] R_data1,
  output [31:0] R_data2
);

  // RegisterFile registerfile_1: pin names not known; wires that end beside it: W_data, CLK, W_Enable, W_address, A1_address, A2_address, R_data1, R_data2

  // Other names for the same wires on the sheet: A1[4:0] = A1_address; A2[4:0] = A2_address; A3[4:0] = W_address;
  //   RD1[31:0] = R_data1; RD2[31:0] = R_data2; WD3[31:0] = W_data; WE3 = W_Enable
endmodule

module \单周期CPU控制器  (
  input  [5:0] opcode,
  input  [5:0] funct,
  output RegWrite,
  output RegDst,
  output ALUSrc,
  output Beq,
  output Bne,
  output MemWrite,
  output MemtoReg,
  output [2:0] ALUControl,
  output Halt
);

  wire ALUSrc_t, and_3_out, and_4_out, and_6_out, and_7_out, and_9_out, and_10_out, and_12_out, and_13_out,
       and_15_out, and_16_out, and_18_out, Beq_t, Bne_t, comparator_1_eq, comparator_2_eq, Halt_t,
       MemtoReg_t, MemWrite_t, not_1_out, not_2_out, not_3_out, not_4_out, not_5_out, not_6_out, not_7_out,
       not_8_out, not_9_out, not_10_out, not_11_out, not_12_out, not_13_out, not_14_out, not_15_out,
       not_16_out, not_17_out, not_18_out, not_19_out, or_5_out, or_7_out, RegWrite_t;
  wire [1:0] ALUOp;
  wire [2:0] ALUControl_t;

  and and_1 (ALUOp[1], ~opcode[5], ~opcode[4], ~opcode[3], ~opcode[2], ~opcode[1], ~opcode[0]);  // AND_Gate
  and and_2 (MemtoReg_t, opcode[5], ~opcode[4], ~opcode[3], ~opcode[2], opcode[1], opcode[0]);  // AND_Gate
  or or_1 (RegWrite_t, ALUOp[1], and_12_out, MemtoReg_t);
  not not_1 (not_1_out, ALUOp[1]);
  not not_2 (not_2_out, funct[4]);
  not not_3 (not_3_out, funct[0]);
  not not_4 (not_4_out, funct[2]);
  and and_3 (and_3_out, not_1_out, ALUOp[0]);
  and and_4 (and_4_out, ALUOp[1], funct[5], not_2_out, not_4_out, funct[1], not_3_out);
  or or_2 (ALUControl_t[2], and_3_out, and_4_out);
  Comparator #(.width(6), .mode("twosComplement")) comparator_1 (
    .a(funct), .b(6'b001100), .eq(comparator_1_eq));  // open: gt, lt
  Comparator #(.width(2), .mode("twosComplement")) comparator_2 (
    .a(ALUOp), .b(2'b10), .eq(comparator_2_eq));  // open: gt, lt
  and and_5 (MemWrite_t, opcode[5], ~opcode[4], opcode[3], ~opcode[2], opcode[1], opcode[0]);  // AND_Gate
  or or_3 (ALUSrc_t, MemtoReg_t, MemWrite_t, and_12_out);
  not not_5 (not_5_out, ALUOp[1]);
  not not_6 (not_6_out, ALUOp[0]);
  and and_6 (and_6_out, not_5_out, not_6_out);
  not not_7 (not_7_out, ALUOp[1]);
  and and_7 (and_7_out, not_7_out, ALUOp[0]);
  or or_4 (ALUControl_t[1], and_6_out, and_7_out, and_10_out);
  and and_8 (Beq_t, ~opcode[5], ~opcode[4], ~opcode[3], opcode[2], ~opcode[1], ~opcode[0]);  // AND_Gate
  not not_8 (not_8_out, funct[0]);
  not not_9 (not_9_out, funct[3]);
  not not_10 (not_10_out, funct[2]);
  not not_11 (not_11_out, funct[4]);
  and and_9 (and_9_out, funct[5], not_11_out, not_9_out, not_10_out, not_8_out);
  and and_10 (and_10_out, ALUOp[1], or_5_out);
  and and_11 (Halt_t, comparator_1_eq, comparator_2_eq);
  and and_12 (and_12_out, ~opcode[5], ~opcode[4], opcode[3], ~opcode[2], ~opcode[1], ~opcode[0]);  // AND_Gate
  not not_12 (not_12_out, funct[4]);
  not not_13 (not_13_out, funct[2]);
  not not_14 (not_14_out, funct[0]);
  and and_13 (and_13_out, funct[5], not_12_out, funct[3], not_13_out, funct[1], not_14_out);
  or or_5 (or_5_out, and_9_out, and_13_out);
  and and_14 (Bne_t, ~opcode[5], ~opcode[4], ~opcode[3], opcode[2], ~opcode[1], opcode[0]);  // AND_Gate
  or or_6 (ALUOp[0], Bne_t, Beq_t);
  not not_15 (not_15_out, funct[4]);
  not not_16 (not_16_out, funct[3]);
  and and_15 (and_15_out, ALUOp[1], funct[5], not_15_out);
  and and_16 (and_16_out, not_16_out, funct[2], not_19_out, funct[0]);
  and and_17 (ALUControl_t[0], and_15_out, or_7_out);
  not not_17 (not_17_out, funct[2]);
  not not_18 (not_18_out, funct[0]);
  not not_19 (not_19_out, funct[1]);
  and and_18 (and_18_out, funct[3], not_17_out, funct[1], not_18_out);
  or or_7 (or_7_out, and_16_out, and_18_out);
  assign {RegWrite, RegDst, ALUSrc, Beq, Bne, MemWrite, MemtoReg, ALUControl, Halt} = {11{1'b0}} | {RegWrite_t, ALUOp[1], ALUSrc_t, Beq_t, Bne_t, MemWrite_t, MemtoReg_t, ALUControl_t, Halt_t};  // OR_Gate or_8, 11 bits wide

  // Other names for the same wires on the sheet: RegDst_t = ALUOp[1]
endmodule

module \实验3_单周期处理器  (
);

  wire ALUsrc, and_2_out, and_3_out, Beq, Bne, Clock, Clock_out, Halt, MemtoReg, MemWrite, or_1_out, RegDst,
       RegWrite, Reset, \算术逻辑运算单元alu_1_结果是否为0 ;
  wire [2:0] ALUControl;
  wire [4:0] multiplexer_2_out;
  wire [31:0] adder_1_out, bit_extender_1_out, counter_1_q, \mips寄存器文件_1_r_data1 , \mips寄存器文件_1_r_data2 ,
       multiplexer_1_out, multiplexer_3_out, RAM_data_bus_out, ROM_data_bus_out, shifter_1_out, WD3, \移位相加 ,
       \算术逻辑运算单元alu_1_result ;

  Counter #(.width(32), .max('hffffffff), .ongoal("wrap"), .trigger("rising"), .behavior("new")) counter_1 (
    .load(1'b1), .D(multiplexer_1_out), .Q(counter_1_q), .clk(Clock), .clr(Reset));  // open: count, carry, preset, down
  Multiplexer #(.select(1), .width(32), .disabled("Z"), .enable("false")) multiplexer_1 (
    .in0(adder_1_out), .in1(\移位相加 ), .out(multiplexer_1_out), .sel(or_1_out));
  Button u_Reset (.out(Reset));
  Clock #(.highDuration(1), .lowDuration(1)) u_Clock (.out(Clock_out));
  and and_1 (Clock, Clock_out, ~Halt);  // AND_Gate
  // Probe on ROM_data_bus_out
  \_32位地址总线32位数据总线ROM存储器  ROM (.CS(1'b1), .Address_Bus(counter_1_q), .Data_Bus_Out(ROM_data_bus_out));
  Adder #(.width(32)) adder_1 (.a(counter_1_q), .b(32'h4), .out(adder_1_out));  // open: cin, cout
  Multiplexer #(.select(1), .width(5), .disabled("Z"), .enable("false")) multiplexer_2 (
    .in0(ROM_data_bus_out[20:16]), .in1(ROM_data_bus_out[15:11]), .out(multiplexer_2_out), .sel(RegDst));
  \单周期CPU控制器  \u_单周期cpu控制器_1  (
    .opcode(ROM_data_bus_out[31:26]), .funct(ROM_data_bus_out[5:0]), .RegWrite(RegWrite), .RegDst(RegDst),
    .ALUSrc(ALUsrc), .Beq(Beq), .Bne(Bne), .MemWrite(MemWrite), .MemtoReg(MemtoReg), .ALUControl(ALUControl),
    .Halt(Halt));
  \MIPS寄存器文件  \mips寄存器文件_1  (
    .A1_address(ROM_data_bus_out[25:21]), .W_data(WD3), .R_data1(\mips寄存器文件_1_r_data1 ),
    .R_data2(\mips寄存器文件_1_r_data2 ), .A2_address(ROM_data_bus_out[20:16]), .W_address(multiplexer_2_out),
    .W_Enable(RegWrite), .CLK(Clock));
  assign bit_extender_1_out = {{16{ROM_data_bus_out[15]}}, ROM_data_bus_out[15:0]};  // Bit_Extender bit_extender_1
  or or_1 (or_1_out, and_2_out, and_3_out);
  and and_2 (and_2_out, \算术逻辑运算单元alu_1_结果是否为0 , Beq);
  and and_3 (and_3_out, Bne, ~\算术逻辑运算单元alu_1_结果是否为0 );  // AND_Gate
  Multiplexer #(.select(1), .width(32), .disabled("Z"), .enable("false")) multiplexer_3 (
    .in0(\mips寄存器文件_1_r_data2 ), .in1(bit_extender_1_out), .out(multiplexer_3_out), .sel(ALUsrc));
  \算术逻辑运算单元ALU  \u_算术逻辑运算单元alu_1  (
    .AluOP(ALUControl), .X(\mips寄存器文件_1_r_data1 ), .Result(\算术逻辑运算单元alu_1_result ), .Y(multiplexer_3_out),
    .\结果是否为0 (\算术逻辑运算单元alu_1_结果是否为0 ));
  Shifter #(.width(32), .shift("ll")) shifter_1 (.in(bit_extender_1_out), .\dist (5'b00010), .out(shifter_1_out));
  Adder #(.width(32)) adder_2 (.a(shifter_1_out), .b(adder_1_out), .out(\移位相加 ));  // open: cin, cout
  \_32位地址总线32位数据总线RAM存储器  RAM (
    .CS(1'b1), .Store(MemWrite), .CLK(Clock), .Address_Bus(\算术逻辑运算单元alu_1_result ),
    .Data_Bus_In(\mips寄存器文件_1_r_data2 ), .Load(1'b1), .Clear(1'b0), .Data_Bus_Out(RAM_data_bus_out));
  // Probe on RAM_data_bus_out
  Multiplexer #(.select(1), .width(32), .disabled("Z"), .enable("false")) multiplexer_4 (
    .in0(\算术逻辑运算单元alu_1_result ), .in1(RAM_data_bus_out), .out(WD3), .sel(MemtoReg));
endmodule

module \讨论4_构建算术机器  (
);

  wire ALUsrc, Clock, Clock_out, Halt, RegDst, RegWrite, Reset, Zero;
  wire [2:0] ALUControl;
  wire [4:0] multiplexer_1_out;
  wire [31:0] adder_1_out, bit_extender_1_out, counter_1_q, \mips寄存器文件_1_r_data1 , \mips寄存器文件_1_r_data2 ,
       multiplexer_2_out, ROM_data_bus_out, WD3;

  Button u_Reset (.out(Reset));
  Clock #(.highDuration(1), .lowDuration(1)) u_Clock (.out(Clock_out));
  Counter #(.width(32), .max('hffffffff), .ongoal("wrap"), .trigger("rising"), .behavior("old")) counter_1 (
    .load(1'b1), .D(adder_1_out), .Q(counter_1_q), .clk(Clock), .clr(Reset));  // open: count, carry, preset
  and and_1 (Clock, Clock_out, ~Halt);  // AND_Gate
  // Probe on ROM_data_bus_out
  \_32位地址总线32位数据总线ROM存储器  ROM (.CS(1'b1), .Address_Bus(counter_1_q), .Data_Bus_Out(ROM_data_bus_out));
  Adder #(.width(32)) adder_1 (.a(counter_1_q), .b(32'h4), .out(adder_1_out));  // open: cin, cout
  Multiplexer #(.select(1), .width(5), .disabled("Z"), .enable("false")) multiplexer_1 (
    .in0(ROM_data_bus_out[20:16]), .in1(ROM_data_bus_out[15:11]), .out(multiplexer_1_out), .sel(RegDst));
  \算术机器控制器  \u_算术机器控制器_1  (
    .opcode(ROM_data_bus_out[31:26]), .funct(ROM_data_bus_out[5:0]), .RegWrite(RegWrite), .RegDst(RegDst),
    .ALUSrc(ALUsrc), .ALUControl(ALUControl), .Halt(Halt));
  \MIPS寄存器文件  \mips寄存器文件_1  (
    .A1_address(ROM_data_bus_out[25:21]), .W_data(WD3), .R_data1(\mips寄存器文件_1_r_data1 ),
    .R_data2(\mips寄存器文件_1_r_data2 ), .A2_address(ROM_data_bus_out[20:16]), .W_address(multiplexer_1_out),
    .W_Enable(RegWrite), .CLK(Clock));
  assign bit_extender_1_out = {{16{ROM_data_bus_out[15]}}, ROM_data_bus_out[15:0]};  // Bit_Extender bit_extender_1
  Multiplexer #(.select(1), .width(32), .disabled("Z"), .enable("false")) multiplexer_2 (
    .in0(\mips寄存器文件_1_r_data2 ), .in1(bit_extender_1_out), .out(multiplexer_2_out), .sel(ALUsrc));
  \算术逻辑运算单元ALU  \u_算术逻辑运算单元alu_1  (
    .AluOP(ALUControl), .X(\mips寄存器文件_1_r_data1 ), .Result(WD3), .Y(multiplexer_2_out), .\结果是否为0 (Zero));
endmodule

module \算术机器控制器  (
  input  [5:0] opcode,
  input  [5:0] funct,
  output RegWrite,
  output RegDst,
  output ALUSrc,
  output [2:0] ALUControl,
  output Halt
);

  wire ALUSrc_t, and_2_out, and_3_out, and_4_out, and_5_out, and_6_out, and_7_out, and_8_out, and_9_out,
       and_10_out, and_12_out, and_13_out, and_14_out, and_15_out, and_16_out, and_18_out, comparator_1_eq,
       comparator_2_eq, Halt_t, not_1_out, not_2_out, not_3_out, not_4_out, not_5_out, not_6_out, not_7_out,
       not_8_out, not_9_out, not_10_out, not_11_out, not_12_out, not_13_out, not_14_out, not_15_out,
       not_16_out, not_17_out, not_18_out, not_19_out, not_20_out, not_21_out, not_22_out, not_23_out,
       not_24_out, not_25_out, not_26_out, not_27_out, not_28_out, not_29_out, not_30_out, not_31_out,
       not_32_out, not_33_out, not_34_out, not_35_out, or_6_out, or_7_out, RegWrite_t;
  wire [1:0] op;
  wire [2:0] ALUControl_t;

  not not_1 (not_1_out, opcode[3]);
  not not_2 (not_2_out, opcode[2]);
  not not_3 (not_3_out, opcode[5]);
  not not_4 (not_4_out, opcode[4]);
  and and_1 (op[1], not_3_out, not_4_out, not_1_out, not_2_out, not_6_out, not_7_out);
  not not_5 (not_5_out, opcode[4]);
  not not_6 (not_6_out, opcode[1]);
  not not_7 (not_7_out, opcode[0]);
  not not_8 (not_8_out, opcode[3]);
  not not_9 (not_9_out, opcode[2]);
  and and_2 (and_2_out, opcode[5], not_5_out, not_8_out, not_9_out, opcode[1], opcode[0]);
  or or_1 (RegWrite_t, op[1], and_12_out, and_2_out);
  not not_10 (not_10_out, op[1]);
  not not_11 (not_11_out, funct[4]);
  not not_12 (not_12_out, funct[0]);
  not not_13 (not_13_out, funct[2]);
  and and_3 (and_3_out, op[1], funct[5], not_11_out, not_13_out, funct[1], not_12_out);
  and and_4 (and_4_out, not_10_out, op[0]);
  or or_2 (ALUControl_t[2], and_4_out, and_3_out);
  Comparator #(.width(6), .mode("twosComplement")) comparator_1 (
    .a(funct), .b(6'b001100), .eq(comparator_1_eq));  // open: gt, lt
  Comparator #(.width(2), .mode("twosComplement")) comparator_2 (
    .a(op), .b(2'b10), .eq(comparator_2_eq));  // open: gt, lt
  not not_14 (not_14_out, opcode[2]);
  not not_15 (not_15_out, opcode[4]);
  and and_5 (and_5_out, opcode[5], not_15_out, opcode[3], not_14_out, opcode[1], opcode[0]);
  or or_3 (ALUSrc_t, and_2_out, and_5_out, and_12_out);
  not not_16 (not_16_out, op[0]);
  not not_17 (not_17_out, op[1]);
  and and_6 (and_6_out, not_17_out, not_16_out);
  not not_18 (not_18_out, op[1]);
  and and_7 (and_7_out, not_18_out, op[0]);
  or or_4 (ALUControl_t[1], and_6_out, and_7_out, and_10_out);
  not not_19 (not_19_out, opcode[1]);
  not not_20 (not_20_out, opcode[5]);
  not not_21 (not_21_out, opcode[3]);
  not not_22 (not_22_out, opcode[4]);
  and and_8 (and_8_out, not_20_out, not_22_out, not_21_out, opcode[2], not_19_out, not_27_out);
  or or_5 (op[0], and_8_out, and_14_out);
  not not_23 (not_23_out, funct[0]);
  not not_24 (not_24_out, funct[4]);
  not not_25 (not_25_out, funct[3]);
  not not_26 (not_26_out, funct[2]);
  and and_9 (and_9_out, funct[5], not_24_out, not_25_out, not_26_out, not_23_out);
  and and_10 (and_10_out, op[1], or_6_out);
  and and_11 (Halt_t, comparator_1_eq, comparator_2_eq);
  not not_27 (not_27_out, opcode[0]);
  and and_12 (and_12_out, ~opcode[5], ~opcode[4], opcode[3], ~opcode[2], ~opcode[1], ~opcode[0]);  // AND_Gate
  not not_28 (not_28_out, funct[4]);
  not not_29 (not_29_out, funct[2]);
  not not_30 (not_30_out, funct[0]);
  and and_13 (and_13_out, funct[5], not_28_out, funct[3], not_29_out, funct[1], not_30_out);
  or or_6 (or_6_out, and_9_out, and_13_out);
  and and_14 (and_14_out, ~opcode[5], ~opcode[4], ~opcode[3], opcode[2], ~opcode[1], opcode[0]);  // AND_Gate
  not not_31 (not_31_out, funct[4]);
  not not_32 (not_32_out, funct[3]);
  and and_15 (and_15_out, op[1], funct[5], not_31_out);
  and and_16 (and_16_out, not_32_out, funct[2], not_34_out, funct[0]);
  and and_17 (ALUControl_t[0], and_15_out, or_7_out);
  not not_33 (not_33_out, funct[2]);
  not not_34 (not_34_out, funct[1]);
  not not_35 (not_35_out, funct[0]);
  and and_18 (and_18_out, funct[3], not_33_out, funct[1], not_35_out);
  or or_7 (or_7_out, and_16_out, and_18_out);
  assign {RegWrite, RegDst, ALUSrc, ALUControl, Halt} = {7{1'b0}} | {RegWrite_t, op[1], ALUSrc_t, ALUControl_t, Halt_t};  // OR_Gate or_8, 7 bits wide

  // Other names for the same wires on the sheet: RegDst_t = op[1]
endmodule
